// Logisim project tmp.circ as structural Verilog: 19 circuits, main circuit main
// div_low
module main (
  input  clk,
  input  rst,
  input  Jen,
  input  [31:0] Jin,
  output ALUDone0,
  output ALUDone1,
  output InstDone0,
  output InstDone1,
  output [31:0] R1_0,
  output [31:0] R1_1,
  output [31:0] R2_0,
  output [31:0] R2_1,
  output [31:0] R3_0,
  output [31:0] R3_1,
  output [31:0] Jout,
  output [31:0] R4_0,
  output [31:0] R4_1,
  output [31:0] R5_0,
  output [31:0] R5_1,
  output [31:0] R6_0,
  output [31:0] R6_1,
  output [31:0] R7_0,
  output [31:0] R7_1,
  output [31:0] R8_0,
  output [31:0] R8_1,
  output [31:0] R9_0,
  output [31:0] R9_1,
  output [31:0] R10_0,
  output [31:0] R10_1,
  output [31:0] R11_0,
  output [31:0] R11_1,
  output [31:0] R12_0,
  output [31:0] R12_1,
  output [31:0] R13_0,
  output [31:0] R13_1,
  output [31:0] R14_0,
  output [31:0] R14_1,
  output [31:0] R15_0,
  output [31:0] R15_1,
  output [31:0] R16_0,
  output [31:0] R16_1,
  output [31:0] R17_0,
  output [31:0] R17_1,
  output [31:0] R18_0,
  output [31:0] R18_1,
  output [31:0] R19_0,
  output [31:0] R19_1,
  output [31:0] R20_0,
  output [31:0] R20_1,
  output [31:0] R21_0,
  output [31:0] R21_1,
  output [31:0] R22_0,
  output [31:0] R22_1,
  output [31:0] R23_0,
  output [31:0] R23_1,
  output [31:0] R24_0,
  output [31:0] R24_1,
  output [31:0] R25_0,
  output [31:0] R25_1,
  output [31:0] R26_0,
  output [31:0] R26_1,
  output [31:0] R27_0,
  output [31:0] R27_1,
  output [31:0] R28_0,
  output [31:0] R28_1,
  output [31:0] R29_0,
  output [31:0] R29_1,
  output [31:0] R30_0,
  output [31:0] R30_1,
  output [31:0] R31_0,
  output [31:0] R31_1
);

  wire and_1_out, and_2_out, and_3_out, d_ff_1_q, d_ff_2_q, en, or_1_out, Sync0, Sync1, WE0, WE1;
  wire [8:0] Addr0, Addr1, multiplexer_4_out, multiplexer_6_out, multiplexer_7_out, multiplexer_8_out, PC0,
       PC1, register_2_q, register_4_q;
  wire [31:0] Data0, Data1, DataMem, I_cache0_dout, I_cache1_dout, multiplexer_1_out, multiplexer_2_out,
       multiplexer_3_out, multiplexer_5_out, register_1_q, register_3_q;

  Multiplexer #(.width(32)) multiplexer_1 (.in0(DataMem), .in1(multiplexer_1_out), .out(multiplexer_1_out), .sel(clk));
  jtag_ram512 I_cache0 (.clk(clk), .Jen(Jen), .Jin(Jin), .Addr(PC0), .Dout(I_cache0_dout));  // open: Din, Wen, Jout
  cpu CPU0 (
    .clk(clk), .rst(rst), .DataMem(multiplexer_1_out), .Dout(I_cache0_dout), .SyncIn(Sync1), .CPUID(1'b0),
    .ALUDone(ALUDone0), .MemWrite(WE0), .ALUOut(Addr0), .InstDone(InstDone0), .PC(PC0), .SyncOut(Sync0),
    .R1(R1_0), .R2(R2_0), .R3(R3_0), .R4(R4_0), .R5(R5_0), .R6(R6_0), .R7(R7_0), .R8(R8_0), .R9(R9_0),
    .R10(R10_0), .WriteData(Data0), .R11(R11_0), .R12(R12_0), .R13(R13_0), .R14(R14_0), .R15(R15_0),
    .R16(R16_0), .R17(R17_0), .R18(R18_0), .R19(R19_0), .R20(R20_0), .R21(R21_0), .R22(R22_0), .R23(R23_0),
    .R24(R24_0), .R25(R25_0), .R26(R26_0), .R27(R27_0), .R28(R28_0), .R29(R29_0), .R30(R30_0), .R31(R31_0));
  Multiplexer #(.width(32)) multiplexer_2 (.in0(multiplexer_2_out), .in1(DataMem), .out(multiplexer_2_out), .sel(clk));
  jtag_ram512 I_cache1 (.clk(clk), .Jen(Jen), .Jin(Jin), .Addr(PC1), .Dout(I_cache1_dout));  // open: Din, Wen, Jout
  cpu CPU1 (
    .clk(clk), .rst(rst), .DataMem(multiplexer_2_out), .Dout(I_cache1_dout), .SyncIn(Sync0), .CPUID(1'b1),
    .ALUDone(ALUDone1), .MemWrite(WE1), .ALUOut(Addr1), .InstDone(InstDone1), .PC(PC1), .SyncOut(Sync1),
    .R1(R1_1), .R2(R2_1), .R3(R3_1), .R4(R4_1), .R5(R5_1), .R6(R6_1), .R7(R7_1), .R8(R8_1), .R9(R9_1),
    .R10(R10_1), .WriteData(Data1), .R11(R11_1), .R12(R12_1), .R13(R13_1), .R14(R14_1), .R15(R15_1),
    .R16(R16_1), .R17(R17_1), .R18(R18_1), .R19(R19_1), .R20(R20_1), .R21(R21_1), .R22(R22_1), .R23(R23_1),
    .R24(R24_1), .R25(R25_1), .R26(R26_1), .R27(R27_1), .R28(R28_1), .R29(R29_1), .R30(R30_1), .R31(R31_1));
  and and_1 (and_1_out, WE0, WE1);
  Register #(.width(32)) register_1 (.D(Data1), .en(and_1_out), .clk(clk), .Q(register_1_q), .clr(rst));
  and and_2 (and_2_out, WE0, WE1);
  D_Flip_Flop d_ff_1 (.D(WE0), .clk(clk), .Q(d_ff_1_q), .reset(rst));  // open: Qn, preset
  D_Flip_Flop d_ff_2 (.D(WE1), .clk(clk), .Q(d_ff_2_q), .reset(rst));  // open: Qn, preset
  Register #(.width(9)) register_2 (.D(Addr1), .en(and_2_out), .clk(clk), .Q(register_2_q), .clr(rst));
  Multiplexer #(.width(32)) multiplexer_3 (.in0(register_1_q), .in1(Data1), .out(multiplexer_3_out), .sel(WE1));
  and and_3 (and_3_out, d_ff_1_q, d_ff_2_q);
  Multiplexer #(.width(9)) multiplexer_4 (.in0(register_2_q), .in1(Addr1), .out(multiplexer_4_out), .sel(WE1));
  Register #(.width(32)) register_3 (.D(multiplexer_5_out), .en(1'b1), .clk(clk), .Q(register_3_q), .clr(rst));
  Multiplexer #(.width(32)) multiplexer_5 (.in0(multiplexer_3_out), .in1(Data0), .out(multiplexer_5_out), .sel(WE0));
  D_Flip_Flop d_ff_3 (.D(or_1_out), .clk(clk), .Q(en), .reset(rst));  // open: Qn, preset
  or or_1 (or_1_out, WE0, WE1, and_3_out);
  Register #(.width(9)) register_4 (.D(multiplexer_6_out), .clk(clk), .Q(register_4_q), .clr(rst));  // open: en
  Multiplexer #(.width(9)) multiplexer_6 (.in0(multiplexer_4_out), .in1(Addr0), .out(multiplexer_6_out), .sel(WE0));
  Multiplexer #(.width(9)) multiplexer_7 (.in0(Addr0), .in1(Addr1), .out(multiplexer_7_out), .sel(clk));
  Multiplexer #(.width(9)) multiplexer_8 (
    .in0(multiplexer_7_out), .in1(register_4_q), .out(multiplexer_8_out), .sel(en));
  jtag_ram512 D_cache (
    .clk(clk), .Jen(Jen), .Din(register_3_q), .Wen(en), .Addr(multiplexer_8_out), .Jout(Jout), .Dout(DataMem));  // open: Jin
endmodule

module cpu (
  input  clk,
  input  rst,
  input  [31:0] DataMem,
  input  [31:0] Dout,
  input  SyncIn,
  input  CPUID,
  output ALUDone,
  output MemWrite,
  output [8:0] ALUOut,
  output InstDone,
  output [8:0] PC,
  output SyncOut,
  output [31:0] R1,
  output [31:0] R2,
  output [31:0] R3,
  output [31:0] R4,
  output [31:0] R5,
  output [31:0] R6,
  output [31:0] R7,
  output [31:0] R8,
  output [31:0] R9,
  output [31:0] R10,
  output [31:0] WriteData,
  output [31:0] R11,
  output [31:0] R12,
  output [31:0] R13,
  output [31:0] R14,
  output [31:0] R15,
  output [31:0] R16,
  output [31:0] R17,
  output [31:0] R18,
  output [31:0] R19,
  output [31:0] R20,
  output [31:0] R21,
  output [31:0] R22,
  output [31:0] R23,
  output [31:0] R24,
  output [31:0] R25,
  output [31:0] R26,
  output [31:0] R27,
  output [31:0] R28,
  output [31:0] R29,
  output [31:0] R30,
  output [31:0] R31
);

  wire ASrc, comparator_1_lt, comparator_2_eq, comparator_3_eq, HiLoWE, IRWE, isDiv, PCWE, Zero;
  wire [1:0] BSrc, PCSrc;
  wire [2:0] MemtoReg, RegDst;
  wire [3:0] ALUOp;
  wire [4:0] multiplexer_2_out, rd, rs, rt, Shamt;
  wire [5:0] Funct, Opcode;
  wire [15:0] InstDecoder_imm;
  wire [31:0] A, ALUOutHigh, ALUOutLow, bit_extender_1_out, bit_extender_2_out, bit_extender_7_out, High,
       Imm, InstReg_q, Low, MemOut, multiplexer_1_out, multiplexer_3_out, multiplexer_4_out, Neg,
       regf_dread0, regf_dread1, undriven;
  wire [63:0] adder_1_out, bit_extender_5_out, bit_extender_6_out, bit_extender_8_out, multiplexer_5_out;
  wire [63:9] ALUOut_t;

  Register #(.width(32)) HighReg (.D(ALUOutHigh), .en(HiLoWE), .clk(clk), .Q(High), .clr(rst));
  Register #(.width(32)) LowReg (.D(ALUOutLow), .en(HiLoWE), .clk(clk), .Q(Low), .clr(rst));
  assign bit_extender_1_out = {{23{1'b0}}, PC};  // Bit_Extender bit_extender_1
  assign bit_extender_2_out = {{31{1'b0}}, CPUID};  // Bit_Extender bit_extender_2
  Register #(.width(32)) MemoryDataReg (.D(DataMem), .clk(clk), .Q(MemOut), .clr(rst));  // open: en
  Multiplexer #(.select(3), .width(32)) multiplexer_1 (
    .in0({ALUOut_t[31:9], ALUOut}), .in1(MemOut), .in2(High), .in3(Low), .in4(bit_extender_1_out), .in5(Neg),
    .in6(bit_extender_2_out), .out(multiplexer_1_out));  // open: in7, sel
  Register #(.width(32)) InstReg (.D(Dout), .en(IRWE), .clk(clk), .Q(InstReg_q), .clr(rst));
  Multiplexer #(.select(3), .width(5)) multiplexer_2 (
    .in0({5{1'b0}}), .in1(rt), .in2(rs), .in3(rd), .in4({5{1'b1}}), .out(multiplexer_2_out), .sel(RegDst));  // open: in5, in6, in7
  inst_decoder InstDecoder (
    .inst(InstReg_q), .funct(Funct), .imm(InstDecoder_imm), .shamt(Shamt), .rd(rd), .rt(rt), .rs(rs),
    .opcode(Opcode));
  control_unit ControlUnit (
    .zero(Zero), .opcode(Opcode), .clk(clk), .rst(rst), .func(Funct), .syns_in(SyncIn), .inst_we(IRWE),
    .mem_write(MemWrite), .pc_we(PCWE), .write_addr(RegDst), .alu_in2(BSrc), .pc_select(PCSrc),
    .write_data(MemtoReg), .alu_in1(ASrc), .Aluop(ALUOp), .done(InstDone), .we_hilo(HiLoWE),
    .syns_out(SyncOut));
  regfile regf (
    .clk(clk), .rst(rst), .Dwrite(multiplexer_1_out), .Awrite(multiplexer_2_out), .Aread0(rs), .Aread1(rt),
    .Dread0(regf_dread0), .Dread1(regf_dread1), .R1(R1), .R2(R2), .R3(R3), .R4(R4), .R5(R5), .R6(R6),
    .R7(R7), .R8(R8), .R9(R9), .R10(R10), .R11(R11), .R12(R12), .R13(R13), .R14(R14), .R15(R15), .R16(R16),
    .R17(R17), .R18(R18), .R19(R19), .R20(R20), .R21(R21), .R22(R22), .R23(R23), .R24(R24), .R25(R25),
    .R26(R26), .R27(R27), .R28(R28), .R29(R29), .R30(R30), .R31(R31));
  Comparator #(.width(64)) comparator_1 (
    .a({ALUOut_t, ALUOut}), .b({64{1'b0}}), .eq(Zero), .lt(comparator_1_lt));  // open: gt
  assign Imm = {{16{InstDecoder_imm[15]}}, InstDecoder_imm};  // Bit_Extender bit_extender_3
  assign Neg = {{31{1'b0}}, comparator_1_lt};  // Bit_Extender bit_extender_4
  Register #(.width(32)) AReg (.D(regf_dread0), .clk(clk), .Q(A), .clr(rst));  // open: en
  Register #(.width(32)) BReg (.D(regf_dread1), .clk(clk), .Q(WriteData), .clr(rst));  // open: en
  assign bit_extender_5_out = {{55{PC[8]}}, PC};  // Bit_Extender bit_extender_5
  assign bit_extender_6_out = {{32{Imm[31]}}, Imm};  // Bit_Extender bit_extender_6
  assign bit_extender_7_out = {{23{1'b0}}, PC};  // Bit_Extender bit_extender_7
  Multiplexer #(.select(2), .width(32)) multiplexer_3 (
    .in0(WriteData), .in1(32'h1), .in2(Imm), .in3(undriven), .out(multiplexer_3_out), .sel(BSrc));
  Adder #(.width(64)) adder_1 (.a(bit_extender_5_out), .b(bit_extender_6_out), .out(adder_1_out));  // open: cin, cout
  Comparator #(.width(6)) comparator_2 (.a(Opcode), .b({6{1'b0}}), .eq(comparator_2_eq));  // open: gt, lt
  Comparator #(.width(6)) comparator_3 (.a(Funct), .b(6'b011010), .eq(comparator_3_eq));  // open: gt, lt
  Multiplexer #(.width(32)) multiplexer_4 (.in0(A), .in1(bit_extender_7_out), .out(multiplexer_4_out), .sel(ASrc));
  assign bit_extender_8_out = {{32{A[31]}}, A};  // Bit_Extender bit_extender_8
  and and_1 (isDiv, comparator_2_eq, comparator_3_eq);
  Register #(.width(64)) ALUOutReg (
    .D({ALUOutHigh, ALUOutLow}), .en(1'b1), .clk(clk), .Q({ALUOut_t, ALUOut}), .clr(rst));
  Multiplexer #(.select(2), .width(64)) multiplexer_5 (
    .in0(adder_1_out), .in1({ALUOutHigh, ALUOutLow}), .in2(bit_extender_6_out), .in3(bit_extender_8_out),
    .out(multiplexer_5_out), .sel(PCSrc));
  ALU ALUUnit (
    .a(multiplexer_4_out), .b(multiplexer_3_out), .rst(rst), .aluop(ALUOp), .clk(clk),
    .output_inverted(1'b0), .output_inc(1'b0), .done(ALUDone), .res_high(ALUOutHigh), .res_low(ALUOutLow));
  Register #(.width(9)) PCR (.D(multiplexer_5_out[8:0]), .en(PCWE), .clk(clk), .Q(PC), .clr(rst));

  // Other names for the same wires on the sheet: ALUOut_t[8:0] = ALUOut; B[31:0] = WriteData; Done = ALUDone
endmodule

// 4
module control_unit (
  input  zero,
  input  [5:0] opcode,
  input  clk,
  input  rst,
  input  [5:0] func,
  input  syns_in,
  output inst_we,
  output mem_write,
  output pc_we,
  output [2:0] write_addr,
  output [1:0] alu_in2,
  output [1:0] pc_select,
  output [2:0] write_data,
  output alu_in1,
  output [3:0] Aluop,
  output done,
  output we_hilo,
  output syns_out
);

  wire and_1_out, and_2_out, and_3_out, and_4_out, and_5_out, and_6_out, and_7_out, and_8_out, and_9_out,
       and_10_out, and_14_out, and_15_out, and_16_out, and_17_out, and_18_out, and_19_out, and_20_out,
       and_22_out, and_23_out, and_26_out, and_28_out, and_29_out, and_30_out, and_31_out, and_32_out,
       and_33_out, and_35_out, and_36_out, and_37_out, and_38_out, and_39_out, and_40_out, and_42_out,
       and_43_out, and_44_out, and_45_out, and_46_out, and_47_out, and_48_out, and_49_out, and_50_out,
       and_51_out, b1, b2, b3, b4, b5, b6, b7, b8, b9, b11, b12, b13, b14, b16, b17, b18, b19, b20, b21, b22,
       d_ff_6_q, div, div_enter, dive_done, jr, mfhi, mul_1, mul_enter, n0, n1, n2, n3, n4, n5, nf0, nf1,
       nf2, nf3, nf4, nf5, nor_1_out, not_1_out, not_2_out, not_3_out, not_4_out, ns0, ns1, ns2, ns3, ns4,
       or_3_out, or_6_out, or_9_out, or_13_out, or_21_out, or_22_out, or_23_out, or_24_out, or_25_out,
       or_26_out, or_27_out, or_28_out, or_29_out, or_30_out, or_31_out, or_32_out, R_type, s0, s1, s2, s3,
       s4, s_in, xnor_1_out;
  wire [2:0] or_19_out;
  wire [3:0] and_12_out;

  D_Flip_Flop d_ff_1 (.D(ns3), .clk(clk), .Q(s3), .reset(rst));  // open: Qn, preset
  D_Flip_Flop d_ff_2 (.D(ns4), .clk(clk), .Q(s4), .reset(rst));  // open: Qn, preset
  not not_1 (not_1_out, zero);
  D_Flip_Flop d_ff_3 (.D(ns0), .clk(clk), .Q(s0), .reset(rst));  // open: Qn, preset
  and and_1 (and_1_out, b17, zero);
  and and_2 (and_2_out, not_1_out, b18);
  or or_1 (pc_select[0], b21, b22, syns_out, alu_in2[0]);
  or or_2 (pc_select[1], b21, b14, b14);
  and and_3 (and_3_out, func[0], nf1, func[2]);
  and and_4 (and_4_out, nf0, nf2, func[1]);
  or or_3 (or_3_out, mul_enter, d_ff_6_q, div_enter);
  Counter #(.max('h4f)) counter_1 (
    .clr(or_3_out), .load(1'b0), .up(1'b1), .clk(clk), .carry(dive_done));  // open: count, D, Q
  D_Flip_Flop d_ff_4 (.D(ns1), .clk(clk), .Q(s1), .reset(rst));  // open: Qn, preset
  D_Flip_Flop d_ff_5 (.D(ns2), .clk(clk), .Q(s2), .reset(rst));  // open: Qn, preset
  or or_4 (pc_we, alu_in2[0], b14, b14, b21, and_1_out, and_2_out);
  or or_5 (alu_in1, alu_in2[0], b1);
  nor nor_1 (nor_1_out, func[2], func[4], func[5]);
  xnor xnor_1 (xnor_1_out, func[0], func[1]);
  or or_6 (or_6_out, and_3_out, and_4_out);
  D_Flip_Flop d_ff_6 (.D(dive_done), .clk(clk), .Q(d_ff_6_q));  // open: Qn, preset, reset
  and and_5 (and_5_out, nor_1_out, R_type);
  and and_6 (and_6_out, nf5, func[2], xnor_1_out);
  and and_7 (and_7_out, func[5], or_6_out);
  and and_8 (and_8_out, R_type, func[3]);
  or or_7 (write_data[1], b7, b22, b8);
  or or_8 (write_data[2], b20, b22, write_addr[2]);
  or or_9 (or_9_out, func[3], func[4]);
  Decoder #(.enable("false"), .select(5)) decoder_1 (
    .out0(alu_in2[0]), .out1(b1), .out2(b2), .out3(b3), .out4(b4), .out5(b5), .out6(b6), .out7(b7),
    .out8(b8), .out9(b9), .out10(mem_write), .out11(b11), .out12(b12), .out13(b13), .out14(b14),
    .out15(write_addr[2]), .out16(b16), .out17(b17), .out18(b18), .out19(b19), .out20(b20), .out21(b21),
    .out22(b22), .out23(syns_out), .sel({s4, s3, s2, s1, s0}));  // open: out24, out25, out26, out27, out28, out29, out30, out31
  or or_10 (write_addr[1], b7, b3, b22, b8);
  or or_11 (write_addr[0], b12, b20, b13, b3);
  or or_12 (write_data[0], b12, b8, b20);
  and and_9 (and_9_out, R_type, func[2], nf5);
  and and_10 (and_10_out, R_type, func[1], or_9_out);
  or or_13 (or_13_out, and_5_out, and_6_out, and_7_out, and_8_out);
  or or_14 (alu_in2[1], b1, b13, b4, b9, b19);
  or or_15 (and_12_out[3], and_9_out, and_5_out);
  and and_11 (and_12_out[2], R_type, func[2], func[5]);
  or or_16 (and_12_out[1], and_10_out, opcode[5]);
  and and_12 (and_12_out[0], R_type, or_13_out);
  or or_17 (or_19_out[2], b4, b19, b16);
  or or_18 (or_19_out[1], b6, b5);
  Multiplexer #(.select(3), .width(4)) multiplexer_1 (
    .in0(4'b0000), .in1(and_12_out), .in2(4'b0011), .in3(4'b0010), .in4(4'b1001), .in5(4'b0001), .out(Aluop),
    .sel(or_19_out));  // open: in6, in7
  or or_19 (or_19_out[0], b16, b19, b6, b2);
  or or_20 (we_hilo, dive_done, dive_done);
  not not_2 (not_2_out, alu_in2[0]);
  and and_13 (s_in, not_2_out, syns_in);
  and and_14 (and_14_out, func[1], func[5]);
  and and_15 (and_15_out, nf1, func[4]);
  not not_3 (not_3_out, dive_done);
  not not_4 (not_4_out, dive_done);
  or or_21 (or_21_out, func[2], and_14_out, and_15_out);
  and and_16 (and_16_out, opcode[2], n4);
  and and_17 (and_17_out, opcode[3], opcode[1], n0);
  and and_18 (and_18_out, opcode[1], n3);
  and and_19 (and_19_out, opcode[3], n1, n2);
  and and_20 (and_20_out, func[4], func[1], R_type);
  and and_21 (jr, R_type, nf1, func[3]);
  and and_22 (and_22_out, n1, n2, opcode[3]);
  and and_23 (and_23_out, R_type, nf5, nf4, nf2);
  and and_24 (div, R_type, not_3_out, b5);
  and and_25 (mfhi, R_type, func[4], n1);
  and and_26 (and_26_out, opcode[1], n3, n4, n5);
  and and_27 (mul_1, b6, not_4_out);
  and and_28 (and_28_out, opcode[1], n5);
  and and_29 (and_29_out, R_type, or_21_out);
  and and_30 (and_30_out, opcode[5], n3);
  and and_31 (and_31_out, opcode[3], n2, n1);
  and and_32 (and_32_out, opcode[3], n2);
  and and_33 (and_33_out, opcode[1], opcode[0]);
  and and_34 (div_enter, func[4], b1, R_type, func[3]);
  not not_5 (n0, opcode[0]);
  not not_6 (n1, opcode[1]);
  not not_7 (nf0, func[0]);
  and and_35 (and_35_out, opcode[0], opcode[5]);
  and and_36 (and_36_out, b6, dive_done);
  or or_22 (or_22_out, and_30_out, and_31_out);
  not not_8 (n2, opcode[2]);
  or or_23 (or_23_out, opcode[0], opcode[1], opcode[2], opcode[3], opcode[4], opcode[5]);
  not not_9 (nf1, func[1]);
  not not_10 (nf2, func[2]);
  or or_24 (or_24_out, and_16_out, and_17_out, jr);
  or or_25 (or_25_out, and_35_out, and_18_out, and_19_out, and_20_out);
  and and_37 (and_37_out, b9, and_22_out);
  or or_26 (or_26_out, jr, and_23_out, div, 1'b0, mfhi, and_26_out);
  and and_38 (and_38_out, b1, n0, opcode[5]);
  and and_39 (and_39_out, b9, opcode[5]);
  and and_40 (and_40_out, b16, opcode[2], opcode[0], n4);
  or or_27 (or_27_out, 1'b0, and_28_out, and_29_out);
  and and_41 (mul_enter, b1, opcode[4]);
  and and_42 (and_42_out, b9, or_22_out);
  and and_43 (and_43_out, b16, opcode[2], n3, n0);
  and and_44 (and_44_out, b1, or_28_out);
  or or_28 (or_28_out, 1'b0, jr, mfhi, and_32_out, and_33_out, div_enter);
  not not_11 (n3, opcode[3]);
  not not_12 (n4, opcode[4]);
  not not_13 (R_type, or_23_out);
  not not_14 (nf3, func[3]);
  and and_45 (and_45_out, b1, n0, opcode[5]);
  and and_46 (and_46_out, b1, or_24_out);
  or or_29 (or_29_out, b19, mul_1, div_enter, mul_enter);
  and and_47 (and_47_out, b1, or_26_out);
  and and_48 (and_48_out, b1, n0, opcode[5]);
  or or_30 (or_30_out, b4, and_38_out, mul_1);
  and and_49 (and_49_out, b1, or_27_out);
  or or_31 (or_31_out, mul_enter, write_addr[2], and_36_out);
  not not_15 (n5, opcode[5]);
  not not_16 (nf4, func[4]);
  and and_50 (and_50_out, opcode[1], b1, opcode[5], n0);
  not not_17 (nf5, func[5]);
  and and_51 (and_51_out, b1, or_25_out);
  or or_32 (or_32_out, and_50_out, s_in, div);
  or or_33 (ns4, and_45_out, b19, s_in, b16, and_46_out);
  or or_34 (ns3, b9, b11, write_addr[2], and_51_out);
  or or_35 (ns2, or_29_out, write_addr[2], b11, s_in, and_37_out, and_47_out, and_48_out);
  or or_36 (ns1, or_30_out, b2, and_39_out, s_in, and_40_out, and_49_out, or_31_out);
  or or_37 (ns0, or_32_out, b2, b4, and_36_out, and_42_out, and_43_out, and_44_out, alu_in2[0]);

  assign done = alu_in2[0];
  assign inst_we = alu_in2[0];

  // Other names for the same wires on the sheet: b0 = alu_in2[0]; b10 = mem_write; b23 = syns_out; f0 = func[0];
  //   f1 = func[1]; f2 = func[2]; f3 = func[3]; f4 = func[4]; f5 = func[5]; mul_done = dive_done; op0 = opcode[0];
  //   op1 = opcode[1]; op2 = opcode[2]; op3 = opcode[3]; op4 = opcode[4]; op5 = opcode[5];
  //   state[4:0] = {s4, s3, s2, s1, s0}; b15 = write_addr[2]; zero_in = zero
endmodule

module inst_decoder (
  input  [31:0] inst,
  output [5:0] funct,
  output [15:0] imm,
  output [4:0] shamt,
  output [4:0] rd,
  output [4:0] rt,
  output [4:0] rs,
  output [5:0] opcode
);


  assign funct = inst[5:0];
  assign imm = inst[15:0];
  assign opcode = inst[31:26];
  assign rd = inst[15:11];
  assign rs = inst[25:21];
  assign rt = inst[20:16];
  assign shamt = inst[10:6];
endmodule

module ALU (
  input  [31:0] a,
  input  [31:0] b,
  input  rst,
  input  [3:0] aluop,
  input  clk,
  input  output_inverted,
  input  output_inc,
  output done,
  output [31:0] res_high,
  output [31:0] res_low
);

  wire carry_add, comparator_1_lt, comparator_2_eq, comparator_3_eq, comparator_4_eq, div_done, is_div,
       is_mul, mul_done, multiplexer_6_out, not_4_out, not_5_out, not_6_out, or_2_out, or_3_out, or_4_out,
       start;
  wire [3:0] register_1_q;
  wire [31:0] adder_1_out, and_1_out, bit_extender_1_out, bit_extender_2_out, clo_out_clo, clz_out_clo,
       csa_out_add, dividor_quotient, multiplexer_1_out, multiplexer_2_out, multiplexer_3_out,
       multiplier_out_mul_low, not_1_out, not_2_out, or_1_out, out_mul_high, out_sll_high, out_sra_high,
       out_srl_high, register_2_q, register_3_q, remainder, rotr_out_rotr_low, sll0_out_sll_low,
       sra0_out_sra_low, srl0_out_srl_low, xor_1_out;
  wire [63:0] multiplexer_4_out, not_3_out;

  assign not_1_out = ~b;  // NOT_Gate not_1, 32 bits wide
  Adder #(.width(32)) adder_1 (.a(not_1_out), .b(32'h1), .out(adder_1_out));  // open: cin, cout
  Multiplexer #(.width(32)) multiplexer_1 (.in0(b), .in1(adder_1_out), .out(multiplexer_1_out), .sel(aluop[0]));
  assign not_2_out = ~a;  // NOT_Gate not_2, 32 bits wide
  carry_select_adder csa (.a(a), .b(multiplexer_1_out), .out_add(csa_out_add), .carry_add(carry_add));
  mul multiplier (
    .clk(clk), .start(start), .a(a), .b(b), .done(mul_done), .out_mul_low(multiplier_out_mul_low),
    .out_mul_high(out_mul_high));
  div dividor (
    .divisor(b), .clk(clk), .start(start), .dividend(a), .done(div_done), .remainder(remainder),
    .quotient(dividor_quotient));
  count_leading_one clo (.a(a), .out_clo(clo_out_clo));
  count_leading_one clz (.a(not_2_out), .out_clo(clz_out_clo));
  shift_left_logical sll0 (.b(b[4:0]), .a(a), .out_sll_low(sll0_out_sll_low), .out_sll_high(out_sll_high));
  shift_right_logical srl0 (.b(b[4:0]), .a(a), .out_srl_low(srl0_out_srl_low), .out_srl_high(out_srl_high));
  shift_right_arithmetic sra0 (.b(b[4:0]), .a(a), .out_sra_low(sra0_out_sra_low), .out_sra_high(out_sra_high));
  rotate_right rotr (.b(b[4:0]), .a(a), .out_rotr_low(rotr_out_rotr_low));
  Comparator #(.mode("unsigned"), .width(32)) comparator_1 (.a(a), .b(b), .lt(comparator_1_lt));  // open: gt, eq
  assign and_1_out = a & b;  // AND_Gate and_1, 32 bits wide
  assign or_1_out = a | b;  // OR_Gate or_1, 32 bits wide
  assign xor_1_out = a ^ b;  // XOR_Gate xor_1, 32 bits wide
  assign bit_extender_1_out = {{31{1'b0}}, carry_add};  // Bit_Extender bit_extender_1
  assign bit_extender_2_out = {{31{comparator_1_lt}}, comparator_1_lt};  // Bit_Extender bit_extender_2
  Multiplexer #(.select(4), .width(32)) multiplexer_2 (
    .in0(bit_extender_1_out), .in1(bit_extender_2_out), .in2(out_mul_high), .in3(remainder),
    .in4({32{1'b0}}), .in5({32{1'b0}}), .in6({32{1'b0}}), .in7({32{1'b0}}), .in8({32{1'b0}}),
    .in9(out_sll_high), .in10(out_srl_high), .in11(out_sra_high), .in12({32{1'b0}}), .in13({32{1'b0}}),
    .in14({32{1'b0}}), .in15({32{1'b0}}), .out(multiplexer_2_out), .sel(aluop));
  Multiplexer #(.select(4), .width(32)) multiplexer_3 (
    .in0(csa_out_add), .in1(csa_out_add), .in2(multiplier_out_mul_low), .in3(dividor_quotient),
    .in4(and_1_out), .in5(or_1_out), .in6(xor_1_out), .in7(clo_out_clo), .in8(clz_out_clo),
    .in9(sll0_out_sll_low), .in10(srl0_out_srl_low), .in11(sra0_out_sra_low), .in12(rotr_out_rotr_low),
    .in13({32{1'b0}}), .in14({32{1'b0}}), .in15({32{1'b0}}), .out(multiplexer_3_out), .sel(aluop));
  assign not_3_out = ~{multiplexer_2_out, multiplexer_3_out};  // NOT_Gate not_3, 64 bits wide
  Multiplexer #(.width(64)) multiplexer_4 (
    .in0({multiplexer_2_out, multiplexer_3_out}), .in1(not_3_out), .out(multiplexer_4_out),
    .sel(output_inverted));
  Register #(.width(4)) register_1 (.D(aluop), .clk(clk), .Q(register_1_q));  // open: en, clr
  Register #(.width(32)) register_2 (.D(a), .clk(clk), .Q(register_2_q));  // open: en, clr
  Register #(.width(32)) register_3 (.D(b), .clk(clk), .Q(register_3_q));  // open: en, clr
  Adder #(.width(64)) adder_2 (
    .a(multiplexer_4_out), .b({{63{1'b0}}, output_inc}), .out({res_high, res_low}));  // open: cin, cout
  Comparator #(.mode("unsigned"), .width(4)) comparator_2 (
    .a(register_1_q), .b(aluop), .eq(comparator_2_eq));  // open: gt, lt
  Comparator #(.mode("unsigned"), .width(32)) comparator_3 (
    .a(register_2_q), .b(a), .eq(comparator_3_eq));  // open: gt, lt
  Comparator #(.mode("unsigned"), .width(32)) comparator_4 (
    .a(register_3_q), .b(b), .eq(comparator_4_eq));  // open: gt, lt
  not not_4 (not_4_out, comparator_2_eq);
  not not_5 (not_5_out, comparator_3_eq);
  not not_6 (not_6_out, comparator_4_eq);
  or or_2 (or_2_out, not_4_out, not_5_out, not_6_out);
  and and_2 (start, or_2_out, or_3_out);
  or or_3 (or_3_out, is_div, is_mul);
  Comparator #(.width(4)) comparator_5 (.a(aluop), .b(4'b0010), .eq(is_mul));  // open: gt, lt
  Comparator #(.width(4)) comparator_6 (.a(aluop), .b(4'b0011), .eq(is_div));  // open: gt, lt
  Multiplexer multiplexer_5 (.in0(1'b1), .in1(multiplexer_6_out), .out(done), .sel(or_4_out));
  Multiplexer multiplexer_6 (.in0(div_done), .in1(mul_done), .out(multiplexer_6_out), .sel(is_mul));
  or or_4 (or_4_out, is_mul, is_div);
endmodule

module mul (
  input  clk,
  input  start,
  input  [31:0] a,
  input  [31:0] b,
  output done,
  output [31:0] out_mul_low,
  output [31:0] out_mul_high
);

  wire ans_neg, multiplexer_8_out, not_3_out, not_4_out, or_1_out, or_2_out;
  wire [4:0] counter_1_q;
  wire [31:0] a_high_reg_q, a_low_reg_q, adder_1_out, adder_2_out, b_reg_q, csa1_out_high, csa1_out_low,
       csa2_out_low, csa3_out_low, multiplexer_1_out, multiplexer_2_out, multiplexer_3_out,
       multiplexer_4_out, multiplexer_5_out, multiplexer_6_out, multiplexer_7_out, multiplexer_9_out,
       multiplexer_10_out, multiplexer_11_out, multiplexer_12_out, not_1_out, not_2_out, sll0_out_high,
       sll0_out_low, sll1_out_high, sll1_out_low, srl1_out_srl_low;
  wire [63:0] adder_3_out, ans_low_reg_q, not_5_out;

  assign not_1_out = ~a;  // NOT_Gate not_1, 32 bits wide
  xor xor_1 (ans_neg, a[31], b[31]);
  Adder #(.width(32)) adder_1 (.a(not_1_out), .b(32'h1), .out(adder_1_out));  // open: cin, cout
  assign not_2_out = ~b;  // NOT_Gate not_2, 32 bits wide
  Multiplexer #(.width(32)) multiplexer_1 (.in0(a), .in1(adder_1_out), .out(multiplexer_1_out), .sel(a[31]));
  Adder #(.width(32)) adder_2 (.a(not_2_out), .b(32'h1), .out(adder_2_out));  // open: cin, cout
  Multiplexer #(.width(32)) multiplexer_2 (.in0(b), .in1(adder_2_out), .out(multiplexer_2_out), .sel(b[31]));
  Counter #(.max('h1f), .width(5)) counter_1 (
    .clr(1'b0), .load(start), .up(1'b0), .count(1'b1), .clk(clk), .D(5'b01111), .Q(counter_1_q));  // open: carry
  Multiplexer #(.width(32)) multiplexer_3 (
    .in0(a_low_reg_q), .in1(multiplexer_1_out), .out(multiplexer_3_out), .sel(start));
  Multiplexer #(.width(32)) multiplexer_4 (.in0(a_high_reg_q), .in1({32{1'b0}}), .out(multiplexer_4_out), .sel(start));
  Multiplexer #(.width(32)) multiplexer_5 (
    .in0(ans_low_reg_q[31:0]), .in1({32{1'b0}}), .out(multiplexer_5_out), .sel(start));
  Multiplexer #(.width(32)) multiplexer_6 (
    .in0(ans_low_reg_q[63:32]), .in1({32{1'b0}}), .out(multiplexer_6_out), .sel(start));
  Multiplexer #(.width(32)) multiplexer_7 (
    .in0(b_reg_q), .in1(multiplexer_2_out), .out(multiplexer_7_out), .sel(start));
  not not_3 (not_3_out, start);
  or or_1 (or_1_out, counter_1_q[0], counter_1_q[1], counter_1_q[2], counter_1_q[3], counter_1_q[4]);
  not not_4 (not_4_out, or_1_out);
  sll_64 sll0 (
    .in_low(multiplexer_3_out), .in_high(multiplexer_4_out), .out_low(sll0_out_low), .out_high(sll0_out_high));
  or or_2 (or_2_out, not_4_out, done);
  Multiplexer multiplexer_8 (.in0(1'b0), .in1(or_2_out), .out(multiplexer_8_out), .sel(not_3_out));
  Multiplexer #(.width(32)) multiplexer_9 (
    .in0({32{1'b0}}), .in1(multiplexer_3_out), .out(multiplexer_9_out), .sel(multiplexer_7_out[0]));
  Multiplexer #(.width(32)) multiplexer_10 (
    .in0({32{1'b0}}), .in1(multiplexer_4_out), .out(multiplexer_10_out), .sel(multiplexer_7_out[0]));
  Multiplexer #(.width(32)) multiplexer_11 (
    .in0({32{1'b0}}), .in1(sll0_out_low), .out(multiplexer_11_out), .sel(multiplexer_7_out[1]));
  Multiplexer #(.width(32)) multiplexer_12 (
    .in0({32{1'b0}}), .in1(sll0_out_high), .out(multiplexer_12_out), .sel(multiplexer_7_out[1]));
  D_Flip_Flop d_ff_1 (.D(multiplexer_8_out), .clk(clk), .Q(done), .reset(start));  // open: Qn, preset
  sll_64 sll1 (.in_low(sll0_out_low), .in_high(sll0_out_high), .out_low(sll1_out_low), .out_high(sll1_out_high));
  carry_save_adder csa1 (
    .a(multiplexer_9_out), .b(multiplexer_11_out), .c(multiplexer_5_out), .out_low(csa1_out_low),
    .out_high(csa1_out_high));
  carry_save_adder csa2 (
    .a(multiplexer_10_out), .b(multiplexer_12_out), .c(multiplexer_6_out), .out_low(csa2_out_low));  // open: out_high
  carry_save_adder csa3 (
    .a(csa1_out_high), .b(csa2_out_low), .c({32{1'b0}}), .out_low(csa3_out_low));  // open: out_high
  shift_right_logical srl1 (.b(5'b00010), .a(multiplexer_7_out), .out_srl_low(srl1_out_srl_low));  // open: out_srl_high
  Register #(.width(32)) a_low_reg (.D(sll1_out_low), .clk(clk), .Q(a_low_reg_q));  // open: en, clr
  Register #(.width(32)) a_high_reg (.D(sll1_out_high), .clk(clk), .Q(a_high_reg_q));  // open: en, clr
  Register #(.width(32)) ans_low_reg (.D(csa1_out_low), .clk(clk), .Q(ans_low_reg_q[31:0]));  // open: en, clr
  Register #(.width(32)) ans_high_reg (.D(csa3_out_low), .clk(clk), .Q(ans_low_reg_q[63:32]));  // open: en, clr
  Register #(.width(32)) b_reg (.D(srl1_out_srl_low), .clk(clk), .Q(b_reg_q));  // open: en, clr
  assign not_5_out = ~ans_low_reg_q;  // NOT_Gate not_5, 64 bits wide
  Multiplexer #(.width(64)) multiplexer_13 (
    .in0(ans_low_reg_q), .in1(adder_3_out), .out({out_mul_high, out_mul_low}), .sel(ans_neg));
  Adder #(.width(64)) adder_3 (.a(not_5_out), .b(64'h1), .out(adder_3_out));  // open: cin, cout

  // Other names for the same wires on the sheet: a_neg = a[31]; b_neg = b[31]
endmodule

module div (
  input  [31:0] divisor,
  input  clk,
  input  start,
  input  [31:0] dividend,
  output done,
  output [31:0] remainder,
  output [31:0] quotient
);

  wire and_1_out, and_2_out, comparator_1_eq, comparator_2_lt, is_loading, not_1_out, not_3_out, not_4_out,
       or_2_out, or_3_out, or_4_out, or_5_out;
  wire [6:0] ctr;
  wire [31:0] b, multiplexer_1_out, multiplexer_2_out, multiplexer_3_out, multiplexer_4_out,
       multiplexer_5_out, multiplexer_6_out, or_1_out, subtractor_1_out;

  Counter #(.max('h7f), .width(7)) counter_1 (
    .clr(start), .load(is_loading), .up(1'b0), .clk(clk), .D(7'b1000000), .Q(ctr));  // open: count, carry
  Register #(.width(32)) u_b (.D(divisor), .en(start), .clk(clk), .Q(b));  // open: clr
  assign or_1_out = 32'h1 | quotient;  // OR_Gate or_1, 32 bits wide
  or or_2 (or_2_out, ctr[0], ctr[1], ctr[2], ctr[3], ctr[4], ctr[5], ctr[6]);
  Comparator #(.mode("unsigned"), .width(7)) comparator_1 (
    .a(7'b0000001), .b(ctr), .eq(comparator_1_eq));  // open: gt, lt
  Subtractor #(.width(32)) subtractor_1 (.a(remainder), .b(b), .out(subtractor_1_out));  // open: bin, bout
  Comparator #(.mode("unsigned"), .width(32)) comparator_2 (
    .a(remainder), .b(b), .lt(comparator_2_lt));  // open: gt, eq
  not not_1 (not_1_out, comparator_2_lt);
  Multiplexer #(.width(32)) multiplexer_1 (.in0(quotient), .in1(or_1_out), .out(multiplexer_1_out), .sel(not_1_out));
  not not_2 (is_loading, or_2_out);
  D_Flip_Flop d_ff_1 (.D(or_3_out), .clk(clk), .Q(done), .reset(start));  // open: Qn, preset
  or or_3 (or_3_out, comparator_1_eq, done);
  Multiplexer #(.width(32)) multiplexer_2 (
    .in0(remainder), .in1(subtractor_1_out), .out(multiplexer_2_out), .sel(not_1_out));
  Multiplexer #(.width(32)) multiplexer_3 (
    .in0(multiplexer_2_out), .in1({32{1'b0}}), .out(multiplexer_3_out), .sel(is_loading));
  Multiplexer #(.width(32)) multiplexer_4 (
    .in0({remainder[30:0], quotient[31]}), .in1(multiplexer_3_out), .out(multiplexer_4_out), .sel(or_4_out));
  or or_4 (or_4_out, is_loading, ctr[0]);
  not not_3 (not_3_out, done);
  Multiplexer #(.width(32)) multiplexer_5 (
    .in0({quotient[30:0], 1'b0}), .in1(multiplexer_6_out), .out(multiplexer_5_out), .sel(or_5_out));
  Multiplexer #(.width(32)) multiplexer_6 (
    .in0(multiplexer_1_out), .in1(dividend), .out(multiplexer_6_out), .sel(is_loading));
  or or_5 (or_5_out, is_loading, ctr[0]);
  Register #(.width(32)) a (.D(multiplexer_4_out), .en(1'b1), .clk(and_1_out), .Q(remainder));  // open: clr
  and and_1 (and_1_out, not_3_out, clk);
  Register #(.width(32)) q (.D(multiplexer_5_out), .en(1'b1), .clk(and_2_out), .Q(quotient));  // open: clr
  and and_2 (and_2_out, not_4_out, clk);
  not not_4 (not_4_out, done);

  // Other names for the same wires on the sheet: q[31:0] = quotient; a[31:0] = remainder
endmodule

module shift_right_logical (
  input  [4:0] b,
  input  [31:0] a,
  output [31:0] out_srl_low,
  output [31:0] out_srl_high
);

  wire [1:0] multiplexer_3_out, multiplexer_3_out_2, multiplexer_3_out_3, multiplexer_3_out_4,
       multiplexer_3_out_5, multiplexer_3_out_6, multiplexer_3_out_7, multiplexer_3_out_8,
       multiplexer_3_out_9, multiplexer_3_out_10, multiplexer_3_out_11, multiplexer_3_out_12,
       multiplexer_3_out_13, multiplexer_3_out_14, multiplexer_3_out_15, multiplexer_3_out_16,
       multiplexer_3_out_17, multiplexer_3_out_18, multiplexer_3_out_19, multiplexer_3_out_20,
       multiplexer_3_out_21, multiplexer_3_out_22, multiplexer_3_out_23, multiplexer_3_out_24,
       multiplexer_3_out_25, multiplexer_3_out_26, multiplexer_3_out_27, multiplexer_3_out_28,
       multiplexer_3_out_29, multiplexer_3_out_30, multiplexer_3_out_31, multiplexer_3_out_32;
  wire [3:0] multiplexer_2_out, multiplexer_2_out_2, multiplexer_2_out_3, multiplexer_2_out_4,
       multiplexer_2_out_5, multiplexer_2_out_6, multiplexer_2_out_7, multiplexer_2_out_8,
       multiplexer_2_out_9, multiplexer_2_out_10, multiplexer_2_out_11, multiplexer_2_out_12,
       multiplexer_2_out_13, multiplexer_2_out_14, multiplexer_2_out_15, multiplexer_2_out_16;
  wire [7:0] multiplexer_1_out, multiplexer_1_out_2, multiplexer_1_out_3, multiplexer_1_out_4,
       multiplexer_1_out_5, multiplexer_1_out_6, multiplexer_1_out_7, multiplexer_1_out_8;
  wire [63:0] multiplexer_4_out;

  Multiplexer #(.width(64)) multiplexer_1 (
    .in0({{32{1'b0}}, a}), .in1({{48{1'b0}}, a[31:16]}),
    .out({multiplexer_1_out_8, multiplexer_1_out_7, multiplexer_1_out_6, multiplexer_1_out_5, multiplexer_1_out_4, multiplexer_1_out_3, multiplexer_1_out_2, multiplexer_1_out}),
    .sel(b[4]));
  Multiplexer #(.width(64)) multiplexer_2 (
    .in0({multiplexer_1_out_8, multiplexer_1_out_7, multiplexer_1_out_6, multiplexer_1_out_5, multiplexer_1_out_4, multiplexer_1_out_3, multiplexer_1_out_2, multiplexer_1_out}),
    .in1({{8{1'b0}}, multiplexer_1_out_8, multiplexer_1_out_7, multiplexer_1_out_6, multiplexer_1_out_5, multiplexer_1_out_4, multiplexer_1_out_3, multiplexer_1_out_2}),
    .out({multiplexer_2_out_16, multiplexer_2_out_15, multiplexer_2_out_14, multiplexer_2_out_13, multiplexer_2_out_12, multiplexer_2_out_11, multiplexer_2_out_10, multiplexer_2_out_9, multiplexer_2_out_8, multiplexer_2_out_7, multiplexer_2_out_6, multiplexer_2_out_5, multiplexer_2_out_4, multiplexer_2_out_3, multiplexer_2_out_2, multiplexer_2_out}),
    .sel(b[3]));
  Multiplexer #(.width(64)) multiplexer_3 (
    .in0({multiplexer_2_out_16, multiplexer_2_out_15, multiplexer_2_out_14, multiplexer_2_out_13, multiplexer_2_out_12, multiplexer_2_out_11, multiplexer_2_out_10, multiplexer_2_out_9, multiplexer_2_out_8, multiplexer_2_out_7, multiplexer_2_out_6, multiplexer_2_out_5, multiplexer_2_out_4, multiplexer_2_out_3, multiplexer_2_out_2, multiplexer_2_out}),
    .in1({4'b0000, multiplexer_2_out_16, multiplexer_2_out_15, multiplexer_2_out_14, multiplexer_2_out_13, multiplexer_2_out_12, multiplexer_2_out_11, multiplexer_2_out_10, multiplexer_2_out_9, multiplexer_2_out_8, multiplexer_2_out_7, multiplexer_2_out_6, multiplexer_2_out_5, multiplexer_2_out_4, multiplexer_2_out_3, multiplexer_2_out_2}),
    .out({multiplexer_3_out_32, multiplexer_3_out_31, multiplexer_3_out_30, multiplexer_3_out_29, multiplexer_3_out_28, multiplexer_3_out_27, multiplexer_3_out_26, multiplexer_3_out_25, multiplexer_3_out_24, multiplexer_3_out_23, multiplexer_3_out_22, multiplexer_3_out_21, multiplexer_3_out_20, multiplexer_3_out_19, multiplexer_3_out_18, multiplexer_3_out_17, multiplexer_3_out_16, multiplexer_3_out_15, multiplexer_3_out_14, multiplexer_3_out_13, multiplexer_3_out_12, multiplexer_3_out_11, multiplexer_3_out_10, multiplexer_3_out_9, multiplexer_3_out_8, multiplexer_3_out_7, multiplexer_3_out_6, multiplexer_3_out_5, multiplexer_3_out_4, multiplexer_3_out_3, multiplexer_3_out_2, multiplexer_3_out}),
    .sel(b[2]));
  Multiplexer #(.width(64)) multiplexer_4 (
    .in0({multiplexer_3_out_32, multiplexer_3_out_31, multiplexer_3_out_30, multiplexer_3_out_29, multiplexer_3_out_28, multiplexer_3_out_27, multiplexer_3_out_26, multiplexer_3_out_25, multiplexer_3_out_24, multiplexer_3_out_23, multiplexer_3_out_22, multiplexer_3_out_21, multiplexer_3_out_20, multiplexer_3_out_19, multiplexer_3_out_18, multiplexer_3_out_17, multiplexer_3_out_16, multiplexer_3_out_15, multiplexer_3_out_14, multiplexer_3_out_13, multiplexer_3_out_12, multiplexer_3_out_11, multiplexer_3_out_10, multiplexer_3_out_9, multiplexer_3_out_8, multiplexer_3_out_7, multiplexer_3_out_6, multiplexer_3_out_5, multiplexer_3_out_4, multiplexer_3_out_3, multiplexer_3_out_2, multiplexer_3_out}),
    .in1({2'b00, multiplexer_3_out_32, multiplexer_3_out_31, multiplexer_3_out_30, multiplexer_3_out_29, multiplexer_3_out_28, multiplexer_3_out_27, multiplexer_3_out_26, multiplexer_3_out_25, multiplexer_3_out_24, multiplexer_3_out_23, multiplexer_3_out_22, multiplexer_3_out_21, multiplexer_3_out_20, multiplexer_3_out_19, multiplexer_3_out_18, multiplexer_3_out_17, multiplexer_3_out_16, multiplexer_3_out_15, multiplexer_3_out_14, multiplexer_3_out_13, multiplexer_3_out_12, multiplexer_3_out_11, multiplexer_3_out_10, multiplexer_3_out_9, multiplexer_3_out_8, multiplexer_3_out_7, multiplexer_3_out_6, multiplexer_3_out_5, multiplexer_3_out_4, multiplexer_3_out_3, multiplexer_3_out_2}),
    .out(multiplexer_4_out), .sel(b[1]));
  Multiplexer #(.width(64)) multiplexer_5 (
    .in0(multiplexer_4_out), .in1({1'b0, multiplexer_4_out[63:1]}), .out({out_srl_high, out_srl_low}),
    .sel(b[0]));
endmodule

module shift_left_logical (
  input  [4:0] b,
  input  [31:0] a,
  output [31:0] out_sll_low,
  output [31:0] out_sll_high
);

  wire [1:0] multiplexer_3_out, multiplexer_3_out_2, multiplexer_3_out_3, multiplexer_3_out_4,
       multiplexer_3_out_5, multiplexer_3_out_6, multiplexer_3_out_7, multiplexer_3_out_8,
       multiplexer_3_out_9, multiplexer_3_out_10, multiplexer_3_out_11, multiplexer_3_out_12,
       multiplexer_3_out_13, multiplexer_3_out_14, multiplexer_3_out_15, multiplexer_3_out_16,
       multiplexer_3_out_17, multiplexer_3_out_18, multiplexer_3_out_19, multiplexer_3_out_20,
       multiplexer_3_out_21, multiplexer_3_out_22, multiplexer_3_out_23, multiplexer_3_out_24,
       multiplexer_3_out_25, multiplexer_3_out_26, multiplexer_3_out_27, multiplexer_3_out_28,
       multiplexer_3_out_29, multiplexer_3_out_30, multiplexer_3_out_31, multiplexer_3_out_32;
  wire [3:0] multiplexer_2_out, multiplexer_2_out_2, multiplexer_2_out_3, multiplexer_2_out_4,
       multiplexer_2_out_5, multiplexer_2_out_6, multiplexer_2_out_7, multiplexer_2_out_8,
       multiplexer_2_out_9, multiplexer_2_out_10, multiplexer_2_out_11, multiplexer_2_out_12,
       multiplexer_2_out_13, multiplexer_2_out_14, multiplexer_2_out_15, multiplexer_2_out_16;
  wire [7:0] multiplexer_1_out, multiplexer_1_out_2, multiplexer_1_out_3, multiplexer_1_out_4,
       multiplexer_1_out_5, multiplexer_1_out_6, multiplexer_1_out_7, multiplexer_1_out_8;
  wire [63:0] multiplexer_4_out;

  Multiplexer #(.width(64)) multiplexer_1 (
    .in0({{32{1'b0}}, a}), .in1({{16{1'b0}}, a, {16{1'b0}}}),
    .out({multiplexer_1_out, multiplexer_1_out_8, multiplexer_1_out_7, multiplexer_1_out_6, multiplexer_1_out_5, multiplexer_1_out_4, multiplexer_1_out_3, multiplexer_1_out_2}),
    .sel(b[4]));
  Multiplexer #(.width(64)) multiplexer_2 (
    .in0({multiplexer_1_out, multiplexer_1_out_8, multiplexer_1_out_7, multiplexer_1_out_6, multiplexer_1_out_5, multiplexer_1_out_4, multiplexer_1_out_3, multiplexer_1_out_2}),
    .in1({multiplexer_1_out_8, multiplexer_1_out_7, multiplexer_1_out_6, multiplexer_1_out_5, multiplexer_1_out_4, multiplexer_1_out_3, multiplexer_1_out_2, {8{1'b0}}}),
    .out({multiplexer_2_out, multiplexer_2_out_16, multiplexer_2_out_15, multiplexer_2_out_14, multiplexer_2_out_13, multiplexer_2_out_12, multiplexer_2_out_11, multiplexer_2_out_10, multiplexer_2_out_9, multiplexer_2_out_8, multiplexer_2_out_7, multiplexer_2_out_6, multiplexer_2_out_5, multiplexer_2_out_4, multiplexer_2_out_3, multiplexer_2_out_2}),
    .sel(b[3]));
  Multiplexer #(.width(64)) multiplexer_3 (
    .in0({multiplexer_2_out, multiplexer_2_out_16, multiplexer_2_out_15, multiplexer_2_out_14, multiplexer_2_out_13, multiplexer_2_out_12, multiplexer_2_out_11, multiplexer_2_out_10, multiplexer_2_out_9, multiplexer_2_out_8, multiplexer_2_out_7, multiplexer_2_out_6, multiplexer_2_out_5, multiplexer_2_out_4, multiplexer_2_out_3, multiplexer_2_out_2}),
    .in1({multiplexer_2_out_16, multiplexer_2_out_15, multiplexer_2_out_14, multiplexer_2_out_13, multiplexer_2_out_12, multiplexer_2_out_11, multiplexer_2_out_10, multiplexer_2_out_9, multiplexer_2_out_8, multiplexer_2_out_7, multiplexer_2_out_6, multiplexer_2_out_5, multiplexer_2_out_4, multiplexer_2_out_3, multiplexer_2_out_2, 4'b0000}),
    .out({multiplexer_3_out, multiplexer_3_out_32, multiplexer_3_out_31, multiplexer_3_out_30, multiplexer_3_out_29, multiplexer_3_out_28, multiplexer_3_out_27, multiplexer_3_out_26, multiplexer_3_out_25, multiplexer_3_out_24, multiplexer_3_out_23, multiplexer_3_out_22, multiplexer_3_out_21, multiplexer_3_out_20, multiplexer_3_out_19, multiplexer_3_out_18, multiplexer_3_out_17, multiplexer_3_out_16, multiplexer_3_out_15, multiplexer_3_out_14, multiplexer_3_out_13, multiplexer_3_out_12, multiplexer_3_out_11, multiplexer_3_out_10, multiplexer_3_out_9, multiplexer_3_out_8, multiplexer_3_out_7, multiplexer_3_out_6, multiplexer_3_out_5, multiplexer_3_out_4, multiplexer_3_out_3, multiplexer_3_out_2}),
    .sel(b[2]));
  Multiplexer #(.width(64)) multiplexer_4 (
    .in0({multiplexer_3_out, multiplexer_3_out_32, multiplexer_3_out_31, multiplexer_3_out_30, multiplexer_3_out_29, multiplexer_3_out_28, multiplexer_3_out_27, multiplexer_3_out_26, multiplexer_3_out_25, multiplexer_3_out_24, multiplexer_3_out_23, multiplexer_3_out_22, multiplexer_3_out_21, multiplexer_3_out_20, multiplexer_3_out_19, multiplexer_3_out_18, multiplexer_3_out_17, multiplexer_3_out_16, multiplexer_3_out_15, multiplexer_3_out_14, multiplexer_3_out_13, multiplexer_3_out_12, multiplexer_3_out_11, multiplexer_3_out_10, multiplexer_3_out_9, multiplexer_3_out_8, multiplexer_3_out_7, multiplexer_3_out_6, multiplexer_3_out_5, multiplexer_3_out_4, multiplexer_3_out_3, multiplexer_3_out_2}),
    .in1({multiplexer_3_out_32, multiplexer_3_out_31, multiplexer_3_out_30, multiplexer_3_out_29, multiplexer_3_out_28, multiplexer_3_out_27, multiplexer_3_out_26, multiplexer_3_out_25, multiplexer_3_out_24, multiplexer_3_out_23, multiplexer_3_out_22, multiplexer_3_out_21, multiplexer_3_out_20, multiplexer_3_out_19, multiplexer_3_out_18, multiplexer_3_out_17, multiplexer_3_out_16, multiplexer_3_out_15, multiplexer_3_out_14, multiplexer_3_out_13, multiplexer_3_out_12, multiplexer_3_out_11, multiplexer_3_out_10, multiplexer_3_out_9, multiplexer_3_out_8, multiplexer_3_out_7, multiplexer_3_out_6, multiplexer_3_out_5, multiplexer_3_out_4, multiplexer_3_out_3, multiplexer_3_out_2, 2'b00}),
    .out(multiplexer_4_out), .sel(b[1]));
  Multiplexer #(.width(64)) multiplexer_5 (
    .in0(multiplexer_4_out), .in1({multiplexer_4_out[62:0], 1'b0}), .out({out_sll_high, out_sll_low}),
    .sel(b[0]));
endmodule

module shift_right_arithmetic (
  input  [4:0] b,
  input  [31:0] a,
  output [31:0] out_sra_low,
  output [31:0] out_sra_high
);

  wire [0:0] multiplexer_4_out_2;
  wire [1:0] multiplexer_3_out, multiplexer_3_out_2, multiplexer_3_out_3, multiplexer_3_out_4,
       multiplexer_3_out_5, multiplexer_3_out_6, multiplexer_3_out_7, multiplexer_3_out_8,
       multiplexer_3_out_9, multiplexer_3_out_10, multiplexer_3_out_11, multiplexer_3_out_12,
       multiplexer_3_out_13, multiplexer_3_out_14, multiplexer_3_out_15, multiplexer_3_out_16,
       multiplexer_3_out_17, multiplexer_3_out_18, multiplexer_3_out_19, multiplexer_3_out_20,
       multiplexer_3_out_21, multiplexer_3_out_22, multiplexer_3_out_23, multiplexer_3_out_24,
       multiplexer_3_out_25, multiplexer_3_out_26, multiplexer_3_out_27, multiplexer_3_out_28,
       multiplexer_3_out_29, multiplexer_3_out_30, multiplexer_3_out_31, multiplexer_3_out_32;
  wire [3:0] multiplexer_2_out, multiplexer_2_out_2, multiplexer_2_out_3, multiplexer_2_out_4,
       multiplexer_2_out_5, multiplexer_2_out_6, multiplexer_2_out_7, multiplexer_2_out_8,
       multiplexer_2_out_9, multiplexer_2_out_10, multiplexer_2_out_11, multiplexer_2_out_12,
       multiplexer_2_out_13, multiplexer_2_out_14, multiplexer_2_out_15, multiplexer_2_out_16;
  wire [7:0] multiplexer_1_out, multiplexer_1_out_2, multiplexer_1_out_3, multiplexer_1_out_4,
       multiplexer_1_out_5, multiplexer_1_out_6, multiplexer_1_out_7, multiplexer_1_out_8;
  wire [15:0] bit_extender_1_out, bit_extender_1_out_2, bit_extender_1_out_3, bit_extender_1_out_4;
  wire [62:0] multiplexer_4_out;
  wire [63:0] bit_extender_2_out, bit_extender_3_out, bit_extender_4_out, bit_extender_5_out,
       bit_extender_6_out;

  assign {bit_extender_1_out_3, bit_extender_1_out_2, bit_extender_1_out, bit_extender_1_out_4} = {{32{a[31]}}, a};  // Bit_Extender bit_extender_1
  assign bit_extender_2_out = {{16{bit_extender_1_out_3[15]}}, {bit_extender_1_out_3, bit_extender_1_out_2, bit_extender_1_out}};  // Bit_Extender bit_extender_2
  Multiplexer #(.width(64)) multiplexer_1 (
    .in0({bit_extender_1_out_3, bit_extender_1_out_2, bit_extender_1_out, bit_extender_1_out_4}),
    .in1(bit_extender_2_out),
    .out({multiplexer_1_out_7, multiplexer_1_out_6, multiplexer_1_out_5, multiplexer_1_out_4, multiplexer_1_out_3, multiplexer_1_out_2, multiplexer_1_out, multiplexer_1_out_8}),
    .sel(b[4]));
  Multiplexer #(.width(64)) multiplexer_2 (
    .in0({multiplexer_1_out_7, multiplexer_1_out_6, multiplexer_1_out_5, multiplexer_1_out_4, multiplexer_1_out_3, multiplexer_1_out_2, multiplexer_1_out, multiplexer_1_out_8}),
    .in1(bit_extender_3_out),
    .out({multiplexer_2_out_15, multiplexer_2_out_14, multiplexer_2_out_13, multiplexer_2_out_12, multiplexer_2_out_11, multiplexer_2_out_10, multiplexer_2_out_9, multiplexer_2_out_8, multiplexer_2_out_7, multiplexer_2_out_6, multiplexer_2_out_5, multiplexer_2_out_4, multiplexer_2_out_3, multiplexer_2_out_2, multiplexer_2_out, multiplexer_2_out_16}),
    .sel(b[3]));
  assign bit_extender_3_out = {{8{multiplexer_1_out_7[7]}}, {multiplexer_1_out_7, multiplexer_1_out_6, multiplexer_1_out_5, multiplexer_1_out_4, multiplexer_1_out_3, multiplexer_1_out_2, multiplexer_1_out}};  // Bit_Extender bit_extender_3
  Multiplexer #(.width(64)) multiplexer_3 (
    .in0({multiplexer_2_out_15, multiplexer_2_out_14, multiplexer_2_out_13, multiplexer_2_out_12, multiplexer_2_out_11, multiplexer_2_out_10, multiplexer_2_out_9, multiplexer_2_out_8, multiplexer_2_out_7, multiplexer_2_out_6, multiplexer_2_out_5, multiplexer_2_out_4, multiplexer_2_out_3, multiplexer_2_out_2, multiplexer_2_out, multiplexer_2_out_16}),
    .in1(bit_extender_4_out),
    .out({multiplexer_3_out_31, multiplexer_3_out_30, multiplexer_3_out_29, multiplexer_3_out_28, multiplexer_3_out_27, multiplexer_3_out_26, multiplexer_3_out_25, multiplexer_3_out_24, multiplexer_3_out_23, multiplexer_3_out_22, multiplexer_3_out_21, multiplexer_3_out_20, multiplexer_3_out_19, multiplexer_3_out_18, multiplexer_3_out_17, multiplexer_3_out_16, multiplexer_3_out_15, multiplexer_3_out_14, multiplexer_3_out_13, multiplexer_3_out_12, multiplexer_3_out_11, multiplexer_3_out_10, multiplexer_3_out_9, multiplexer_3_out_8, multiplexer_3_out_7, multiplexer_3_out_6, multiplexer_3_out_5, multiplexer_3_out_4, multiplexer_3_out_3, multiplexer_3_out_2, multiplexer_3_out, multiplexer_3_out_32}),
    .sel(b[2]));
  assign bit_extender_4_out = {{4{multiplexer_2_out_15[3]}}, {multiplexer_2_out_15, multiplexer_2_out_14, multiplexer_2_out_13, multiplexer_2_out_12, multiplexer_2_out_11, multiplexer_2_out_10, multiplexer_2_out_9, multiplexer_2_out_8, multiplexer_2_out_7, multiplexer_2_out_6, multiplexer_2_out_5, multiplexer_2_out_4, multiplexer_2_out_3, multiplexer_2_out_2, multiplexer_2_out}};  // Bit_Extender bit_extender_4
  Multiplexer #(.width(64)) multiplexer_4 (
    .in0({multiplexer_3_out_31, multiplexer_3_out_30, multiplexer_3_out_29, multiplexer_3_out_28, multiplexer_3_out_27, multiplexer_3_out_26, multiplexer_3_out_25, multiplexer_3_out_24, multiplexer_3_out_23, multiplexer_3_out_22, multiplexer_3_out_21, multiplexer_3_out_20, multiplexer_3_out_19, multiplexer_3_out_18, multiplexer_3_out_17, multiplexer_3_out_16, multiplexer_3_out_15, multiplexer_3_out_14, multiplexer_3_out_13, multiplexer_3_out_12, multiplexer_3_out_11, multiplexer_3_out_10, multiplexer_3_out_9, multiplexer_3_out_8, multiplexer_3_out_7, multiplexer_3_out_6, multiplexer_3_out_5, multiplexer_3_out_4, multiplexer_3_out_3, multiplexer_3_out_2, multiplexer_3_out, multiplexer_3_out_32}),
    .in1(bit_extender_5_out), .out({multiplexer_4_out, multiplexer_4_out_2[0]}), .sel(b[1]));
  assign bit_extender_5_out = {{2{multiplexer_3_out_31[1]}}, {multiplexer_3_out_31, multiplexer_3_out_30, multiplexer_3_out_29, multiplexer_3_out_28, multiplexer_3_out_27, multiplexer_3_out_26, multiplexer_3_out_25, multiplexer_3_out_24, multiplexer_3_out_23, multiplexer_3_out_22, multiplexer_3_out_21, multiplexer_3_out_20, multiplexer_3_out_19, multiplexer_3_out_18, multiplexer_3_out_17, multiplexer_3_out_16, multiplexer_3_out_15, multiplexer_3_out_14, multiplexer_3_out_13, multiplexer_3_out_12, multiplexer_3_out_11, multiplexer_3_out_10, multiplexer_3_out_9, multiplexer_3_out_8, multiplexer_3_out_7, multiplexer_3_out_6, multiplexer_3_out_5, multiplexer_3_out_4, multiplexer_3_out_3, multiplexer_3_out_2, multiplexer_3_out}};  // Bit_Extender bit_extender_5
  assign bit_extender_6_out = {{1{multiplexer_4_out[62]}}, multiplexer_4_out};  // Bit_Extender bit_extender_6
  Multiplexer #(.width(64)) multiplexer_5 (
    .in0({multiplexer_4_out, multiplexer_4_out_2[0]}), .in1(bit_extender_6_out),
    .out({out_sra_high, out_sra_low}), .sel(b[0]));
endmodule

module rotate_right (
  input  [4:0] b,
  input  [31:0] a,
  output [31:0] out_rotr_low
);

  wire [4:0] adder_1_out, subtractor_1_out;
  wire [31:0] sll_rotr_out_sll_low, srl_rotr_out_srl_low;

  Subtractor #(.width(5)) subtractor_1 (.a({5{1'b1}}), .b(b), .out(subtractor_1_out));  // open: bin, bout
  Adder #(.width(5)) adder_1 (.a(subtractor_1_out), .b(5'b00001), .out(adder_1_out));  // open: cin, cout
  shift_left_logical sll_rotr (.b(adder_1_out), .a(a), .out_sll_low(sll_rotr_out_sll_low));  // open: out_sll_high
  shift_right_logical srl_rotr (.b(b), .a(a), .out_srl_low(srl_rotr_out_srl_low));  // open: out_srl_high
  assign out_rotr_low = sll_rotr_out_sll_low | srl_rotr_out_srl_low;  // OR_Gate or_1, 32 bits wide
endmodule

module count_leading_one (
  input  [31:0] a,
  output [31:0] out_clo
);

  wire multiplexer_5_out;
  wire [1:0] multiplexer_4_out;
  wire [3:0] multiplexer_3_out;
  wire [4:1] comparator_4_eq;
  wire [5:0] adder_1_out, bit_extender_1_out;
  wire [7:0] multiplexer_2_out;
  wire [15:0] multiplexer_1_out;

  Comparator #(.mode("unsigned"), .width(16)) comparator_1 (
    .a(a[31:16]), .b({16{1'b1}}), .eq(comparator_4_eq[4]));  // open: gt, lt
  Multiplexer #(.width(16)) multiplexer_1 (
    .in0(a[31:16]), .in1(a[15:0]), .out(multiplexer_1_out), .sel(comparator_4_eq[4]));
  Comparator #(.mode("unsigned")) comparator_2 (
    .a(multiplexer_1_out[15:8]), .b({8{1'b1}}), .eq(comparator_4_eq[3]));  // open: gt, lt
  Multiplexer #(.width(8)) multiplexer_2 (
    .in0(multiplexer_1_out[15:8]), .in1(multiplexer_1_out[7:0]), .out(multiplexer_2_out),
    .sel(comparator_4_eq[3]));
  Comparator #(.mode("unsigned"), .width(4)) comparator_3 (
    .a(multiplexer_2_out[7:4]), .b(4'b1111), .eq(comparator_4_eq[2]));  // open: gt, lt
  Multiplexer #(.width(4)) multiplexer_3 (
    .in0(multiplexer_2_out[7:4]), .in1(multiplexer_2_out[3:0]), .out(multiplexer_3_out),
    .sel(comparator_4_eq[2]));
  Comparator #(.mode("unsigned"), .width(2)) comparator_4 (
    .a(multiplexer_3_out[3:2]), .b(2'b11), .eq(comparator_4_eq[1]));  // open: gt, lt
  Multiplexer #(.width(2)) multiplexer_4 (
    .in0(multiplexer_3_out[3:2]), .in1(multiplexer_3_out[1:0]), .out(multiplexer_4_out),
    .sel(comparator_4_eq[1]));
  Multiplexer multiplexer_5 (
    .in0(multiplexer_4_out[1]), .in1(multiplexer_4_out[0]), .out(multiplexer_5_out),
    .sel(multiplexer_4_out[1]));
  Adder #(.width(6)) adder_1 (
    .a({1'b0, comparator_4_eq, multiplexer_4_out[1]}), .b(bit_extender_1_out), .out(adder_1_out));  // open: cin, cout
  assign bit_extender_1_out = {{5{1'b0}}, multiplexer_5_out};  // Bit_Extender bit_extender_1
  assign out_clo = {{26{1'b0}}, adder_1_out};  // Bit_Extender bit_extender_2
endmodule

module carry_select_adder (
  input  [31:0] a,
  input  [31:0] b,
  output [31:0] out_add,
  output carry_add
);

  wire adder_1_cout, adder_2_cout, adder_3_cout, adder_4_cout, adder_5_cout, adder_6_cout, adder_7_cout,
       adder_8_cout, adder_9_cout, adder_10_cout, adder_11_cout, adder_12_cout, adder_13_cout, adder_14_cout,
       adder_15_cout, multiplexer_2_out, multiplexer_4_out, multiplexer_6_out, multiplexer_8_out,
       multiplexer_10_out, multiplexer_12_out;
  wire [3:0] adder_2_out, adder_3_out, adder_4_out, adder_5_out, adder_6_out, adder_7_out, adder_8_out,
       adder_9_out, adder_10_out, adder_11_out, adder_12_out, adder_13_out, adder_14_out, adder_15_out;

  Adder #(.width(4)) adder_1 (.a(a[3:0]), .b(b[3:0]), .out(out_add[3:0]), .cin(1'b0), .cout(adder_1_cout));
  Multiplexer #(.width(4)) multiplexer_1 (.in0(adder_2_out), .in1(adder_3_out), .out(out_add[7:4]), .sel(adder_1_cout));
  Adder #(.width(4)) adder_2 (.a(a[7:4]), .b(b[7:4]), .out(adder_2_out), .cin(1'b0), .cout(adder_2_cout));
  Multiplexer multiplexer_2 (.in0(adder_2_cout), .in1(adder_3_cout), .out(multiplexer_2_out), .sel(adder_1_cout));
  Adder #(.width(4)) adder_3 (.a(a[7:4]), .b(b[7:4]), .out(adder_3_out), .cin(1'b1), .cout(adder_3_cout));
  Multiplexer #(.width(4)) multiplexer_3 (
    .in0(adder_4_out), .in1(adder_5_out), .out(out_add[11:8]), .sel(multiplexer_2_out));
  Adder #(.width(4)) adder_4 (.a(a[11:8]), .b(b[11:8]), .out(adder_4_out), .cin(1'b0), .cout(adder_4_cout));
  Multiplexer multiplexer_4 (.in0(adder_4_cout), .in1(adder_5_cout), .out(multiplexer_4_out), .sel(multiplexer_2_out));
  Adder #(.width(4)) adder_5 (.a(a[11:8]), .b(b[11:8]), .out(adder_5_out), .cin(1'b1), .cout(adder_5_cout));
  Multiplexer #(.width(4)) multiplexer_5 (
    .in0(adder_6_out), .in1(adder_7_out), .out(out_add[15:12]), .sel(multiplexer_4_out));
  Adder #(.width(4)) adder_6 (.a(a[15:12]), .b(b[15:12]), .out(adder_6_out), .cin(1'b0), .cout(adder_6_cout));
  Multiplexer multiplexer_6 (.in0(adder_6_cout), .in1(adder_7_cout), .out(multiplexer_6_out), .sel(multiplexer_4_out));
  Adder #(.width(4)) adder_7 (.a(a[15:12]), .b(b[15:12]), .out(adder_7_out), .cin(1'b1), .cout(adder_7_cout));
  Multiplexer #(.width(4)) multiplexer_7 (
    .in0(adder_8_out), .in1(adder_9_out), .out(out_add[19:16]), .sel(multiplexer_6_out));
  Adder #(.width(4)) adder_8 (.a(a[19:16]), .b(b[19:16]), .out(adder_8_out), .cin(1'b0), .cout(adder_8_cout));
  Multiplexer multiplexer_8 (.in0(adder_8_cout), .in1(adder_9_cout), .out(multiplexer_8_out), .sel(multiplexer_6_out));
  Adder #(.width(4)) adder_9 (.a(a[19:16]), .b(b[19:16]), .out(adder_9_out), .cin(1'b1), .cout(adder_9_cout));
  Multiplexer #(.width(4)) multiplexer_9 (
    .in0(adder_10_out), .in1(adder_11_out), .out(out_add[23:20]), .sel(multiplexer_8_out));
  Adder #(.width(4)) adder_10 (.a(a[23:20]), .b(b[23:20]), .out(adder_10_out), .cin(1'b0), .cout(adder_10_cout));
  Multiplexer multiplexer_10 (
    .in0(adder_10_cout), .in1(adder_11_cout), .out(multiplexer_10_out), .sel(multiplexer_8_out));
  Adder #(.width(4)) adder_11 (.a(a[23:20]), .b(b[23:20]), .out(adder_11_out), .cin(1'b1), .cout(adder_11_cout));
  Multiplexer #(.width(4)) multiplexer_11 (
    .in0(adder_12_out), .in1(adder_13_out), .out(out_add[27:24]), .sel(multiplexer_10_out));
  Adder #(.width(4)) adder_12 (.a(a[27:24]), .b(b[27:24]), .out(adder_12_out), .cin(1'b0), .cout(adder_12_cout));
  Multiplexer multiplexer_12 (
    .in0(adder_12_cout), .in1(adder_13_cout), .out(multiplexer_12_out), .sel(multiplexer_10_out));
  Adder #(.width(4)) adder_13 (.a(a[27:24]), .b(b[27:24]), .out(adder_13_out), .cin(1'b1), .cout(adder_13_cout));
  Multiplexer #(.width(4)) multiplexer_13 (
    .in0(adder_14_out), .in1(adder_15_out), .out(out_add[31:28]), .sel(multiplexer_12_out));
  Adder #(.width(4)) adder_14 (.a(a[31:28]), .b(b[31:28]), .out(adder_14_out), .cin(1'b0), .cout(adder_14_cout));
  Multiplexer multiplexer_14 (.in0(adder_14_cout), .in1(adder_15_cout), .out(carry_add), .sel(multiplexer_12_out));
  Adder #(.width(4)) adder_15 (.a(a[31:28]), .b(b[31:28]), .out(adder_15_out), .cin(1'b1), .cout(adder_15_cout));
endmodule

module carry_save_adder (
  input  [31:0] a,
  input  [31:0] b,
  input  [31:0] c,
  output [31:0] out_low,
  output [31:0] out_high
);

  wire csa_carry_add;
  wire [1:0] xor_3_out;
  wire [31:0] and_1_out, and_2_out, or_1_out, xor_1_out, xor_2_out;

  assign xor_1_out = a ^ b;  // XOR_Gate xor_1, 32 bits wide
  assign and_1_out = a & b;  // AND_Gate and_1, 32 bits wide
  assign xor_2_out = xor_1_out ^ c;  // XOR_Gate xor_2, 32 bits wide
  assign and_2_out = xor_1_out & c;  // AND_Gate and_2, 32 bits wide
  assign or_1_out = and_1_out | and_2_out;  // OR_Gate or_1, 32 bits wide
  carry_select_adder csa (.a(xor_2_out), .b({or_1_out[30:0], 1'b0}), .out_add(out_low), .carry_add(csa_carry_add));
  xor xor_3 (xor_3_out[0], csa_carry_add, or_1_out[31]);
  and and_3 (xor_3_out[1], csa_carry_add, or_1_out[31]);
  assign out_high = {{30{1'b0}}, xor_3_out};  // Bit_Extender bit_extender_1
endmodule

module sll_64 (
  input  [31:0] in_low,
  input  [31:0] in_high,
  output [31:0] out_low,
  output [31:0] out_high
);


  assign out_high = {in_high[30:0], in_low[31]};
  assign out_low = {in_low[30:0], 1'b0};
endmodule

module jtag_ram8 (
  input  clk,
  input  Jen,
  input  [31:0] Din,
  input  [31:0] Jin,
  input  Wen,
  input  [2:0] Addr,
  output [31:0] Dout,
  output [31:0] Jout
);

  wire decoder_1_out0, decoder_1_out1, decoder_1_out2, decoder_1_out3, decoder_1_out4, decoder_1_out5,
       decoder_1_out6, decoder_1_out7, or_1_out, or_2_out, or_3_out, or_4_out, or_5_out, or_6_out, or_7_out,
       or_8_out;
  wire [31:0] M0, M1, M2, M3, M4, M5, M6, multiplexer_1_out, multiplexer_2_out, multiplexer_3_out,
       multiplexer_4_out, multiplexer_5_out, multiplexer_6_out, multiplexer_7_out, multiplexer_8_out;

  Decoder #(.select(3)) decoder_1 (
    .out0(decoder_1_out0), .out1(decoder_1_out1), .out2(decoder_1_out2), .out3(decoder_1_out3),
    .out4(decoder_1_out4), .out5(decoder_1_out5), .out6(decoder_1_out6), .out7(decoder_1_out7), .sel(Addr),
    .en(Wen));
  Multiplexer #(.width(32)) multiplexer_1 (.in0(Din), .in1(Jin), .out(multiplexer_1_out), .sel(Jen));
  Multiplexer #(.width(32)) multiplexer_2 (.in0(Din), .in1(M0), .out(multiplexer_2_out), .sel(Jen));
  Multiplexer #(.width(32)) multiplexer_3 (.in0(Din), .in1(M1), .out(multiplexer_3_out), .sel(Jen));
  Multiplexer #(.width(32)) multiplexer_4 (.in0(Din), .in1(M2), .out(multiplexer_4_out), .sel(Jen));
  Multiplexer #(.width(32)) multiplexer_5 (.in0(Din), .in1(M3), .out(multiplexer_5_out), .sel(Jen));
  Multiplexer #(.width(32)) multiplexer_6 (.in0(Din), .in1(M4), .out(multiplexer_6_out), .sel(Jen));
  Multiplexer #(.width(32)) multiplexer_7 (.in0(Din), .in1(M5), .out(multiplexer_7_out), .sel(Jen));
  Multiplexer #(.width(32)) multiplexer_8 (.in0(Din), .in1(M6), .out(multiplexer_8_out), .sel(Jen));
  Register #(.width(32)) register_1 (.D(multiplexer_1_out), .en(or_1_out), .clk(clk), .Q(M0));  // open: clr
  or or_1 (or_1_out, Jen, decoder_1_out0);
  Register #(.width(32)) register_2 (.D(multiplexer_2_out), .en(or_2_out), .clk(clk), .Q(M1));  // open: clr
  or or_2 (or_2_out, Jen, decoder_1_out1);
  Register #(.width(32)) register_3 (.D(multiplexer_3_out), .en(or_3_out), .clk(clk), .Q(M2));  // open: clr
  or or_3 (or_3_out, Jen, decoder_1_out2);
  Register #(.width(32)) register_4 (.D(multiplexer_4_out), .en(or_4_out), .clk(clk), .Q(M3));  // open: clr
  or or_4 (or_4_out, Jen, decoder_1_out3);
  Register #(.width(32)) register_5 (.D(multiplexer_5_out), .en(or_5_out), .clk(clk), .Q(M4));  // open: clr
  or or_5 (or_5_out, Jen, decoder_1_out4);
  Register #(.width(32)) register_6 (.D(multiplexer_6_out), .en(or_6_out), .clk(clk), .Q(M5));  // open: clr
  or or_6 (or_6_out, Jen, decoder_1_out5);
  Register #(.width(32)) register_7 (.D(multiplexer_7_out), .en(or_7_out), .clk(clk), .Q(M6));  // open: clr
  or or_7 (or_7_out, Jen, decoder_1_out6);
  Register #(.width(32)) register_8 (.D(multiplexer_8_out), .en(or_8_out), .clk(clk), .Q(Jout));  // open: clr
  or or_8 (or_8_out, Jen, decoder_1_out7);
  Multiplexer #(.select(3), .width(32)) multiplexer_9 (
    .in0(M0), .in1(M1), .in2(M2), .in3(M3), .in4(M4), .in5(M5), .in6(M6), .in7(Jout), .out(Dout), .sel(Addr));

  // Other names for the same wires on the sheet: M7[31:0] = Jout
endmodule

module jtag_ram64 (
  input  clk,
  input  Jen,
  input  [31:0] Din,
  input  [31:0] Jin,
  input  Wen,
  input  [5:0] Addr,
  output [31:0] Dout,
  output [31:0] Jout
);

  wire decoder_1_out0, decoder_1_out1, decoder_1_out2, decoder_1_out3, decoder_1_out4, decoder_1_out5,
       decoder_1_out6, decoder_1_out7;
  wire [31:0] b0_dout, b0_jout, b1_dout, b1_jout, b2_dout, b2_jout, b3_dout, b3_jout, b4_dout, b4_jout,
       b5_dout, b5_jout, b6_dout, b6_jout, b7_dout;

  Decoder #(.select(3)) decoder_1 (
    .out0(decoder_1_out0), .out1(decoder_1_out1), .out2(decoder_1_out2), .out3(decoder_1_out3),
    .out4(decoder_1_out4), .out5(decoder_1_out5), .out6(decoder_1_out6), .out7(decoder_1_out7),
    .sel(Addr[5:3]), .en(Wen));
  jtag_ram8 b0 (
    .clk(clk), .Jen(Jen), .Din(Din), .Jin(Jin), .Wen(decoder_1_out0), .Addr(Addr[2:0]), .Dout(b0_dout),
    .Jout(b0_jout));
  jtag_ram8 b1 (
    .clk(clk), .Jen(Jen), .Din(Din), .Jin(b0_jout), .Wen(decoder_1_out1), .Addr(Addr[2:0]), .Dout(b1_dout),
    .Jout(b1_jout));
  jtag_ram8 b2 (
    .clk(clk), .Jen(Jen), .Din(Din), .Jin(b1_jout), .Wen(decoder_1_out2), .Addr(Addr[2:0]), .Dout(b2_dout),
    .Jout(b2_jout));
  jtag_ram8 b3 (
    .clk(clk), .Jen(Jen), .Din(Din), .Jin(b2_jout), .Wen(decoder_1_out3), .Addr(Addr[2:0]), .Dout(b3_dout),
    .Jout(b3_jout));
  jtag_ram8 b4 (
    .clk(clk), .Jen(Jen), .Din(Din), .Jin(b3_jout), .Wen(decoder_1_out4), .Addr(Addr[2:0]), .Dout(b4_dout),
    .Jout(b4_jout));
  jtag_ram8 b5 (
    .clk(clk), .Jen(Jen), .Din(Din), .Jin(b4_jout), .Wen(decoder_1_out5), .Addr(Addr[2:0]), .Dout(b5_dout),
    .Jout(b5_jout));
  jtag_ram8 b6 (
    .clk(clk), .Jen(Jen), .Din(Din), .Jin(b5_jout), .Wen(decoder_1_out6), .Addr(Addr[2:0]), .Dout(b6_dout),
    .Jout(b6_jout));
  jtag_ram8 b7 (
    .clk(clk), .Jen(Jen), .Din(Din), .Jin(b6_jout), .Wen(decoder_1_out7), .Addr(Addr[2:0]), .Dout(b7_dout),
    .Jout(Jout));
  Multiplexer #(.select(3), .width(32)) multiplexer_1 (
    .in0(b0_dout), .in1(b1_dout), .in2(b2_dout), .in3(b3_dout), .in4(b4_dout), .in5(b5_dout), .in6(b6_dout),
    .in7(b7_dout), .out(Dout), .sel(Addr[5:3]));
endmodule

module jtag_ram512 (
  input  clk,
  input  Jen,
  input  [31:0] Din,
  input  [31:0] Jin,
  input  Wen,
  input  [8:0] Addr,
  output [31:0] Jout,
  output [31:0] Dout
);

  wire decoder_1_out0, decoder_1_out1, decoder_1_out2, decoder_1_out3, decoder_1_out4, decoder_1_out5,
       decoder_1_out6, decoder_1_out7;
  wire [31:0] b0_dout, b0_jout, b1_dout, b1_jout, b2_dout, b2_jout, b3_dout, b3_jout, b4_dout, b4_jout,
       b5_dout, b5_jout, b6_dout, b6_jout, b7_dout;

  Decoder #(.select(3)) decoder_1 (
    .out0(decoder_1_out0), .out1(decoder_1_out1), .out2(decoder_1_out2), .out3(decoder_1_out3),
    .out4(decoder_1_out4), .out5(decoder_1_out5), .out6(decoder_1_out6), .out7(decoder_1_out7),
    .sel(Addr[8:6]), .en(Wen));
  jtag_ram64 b0 (
    .clk(clk), .Jen(Jen), .Din(Din), .Jin(Jin), .Wen(decoder_1_out0), .Addr(Addr[5:0]), .Dout(b0_dout),
    .Jout(b0_jout));
  jtag_ram64 b1 (
    .clk(clk), .Jen(Jen), .Din(Din), .Jin(b0_jout), .Wen(decoder_1_out1), .Addr(Addr[5:0]), .Dout(b1_dout),
    .Jout(b1_jout));
  jtag_ram64 b2 (
    .clk(clk), .Jen(Jen), .Din(Din), .Jin(b1_jout), .Wen(decoder_1_out2), .Addr(Addr[5:0]), .Dout(b2_dout),
    .Jout(b2_jout));
  jtag_ram64 b3 (
    .clk(clk), .Jen(Jen), .Din(Din), .Jin(b2_jout), .Wen(decoder_1_out3), .Addr(Addr[5:0]), .Dout(b3_dout),
    .Jout(b3_jout));
  jtag_ram64 b4 (
    .clk(clk), .Jen(Jen), .Din(Din), .Jin(b3_jout), .Wen(decoder_1_out4), .Addr(Addr[5:0]), .Dout(b4_dout),
    .Jout(b4_jout));
  jtag_ram64 b5 (
    .clk(clk), .Jen(Jen), .Din(Din), .Jin(b4_jout), .Wen(decoder_1_out5), .Addr(Addr[5:0]), .Dout(b5_dout),
    .Jout(b5_jout));
  jtag_ram64 b6 (
    .clk(clk), .Jen(Jen), .Din(Din), .Jin(b5_jout), .Wen(decoder_1_out6), .Addr(Addr[5:0]), .Dout(b6_dout),
    .Jout(b6_jout));
  jtag_ram64 b7 (
    .clk(clk), .Jen(Jen), .Din(Din), .Jin(b6_jout), .Wen(decoder_1_out7), .Addr(Addr[5:0]), .Dout(b7_dout),
    .Jout(Jout));
  Multiplexer #(.select(3), .width(32)) multiplexer_1 (
    .in0(b0_dout), .in1(b1_dout), .in2(b2_dout), .in3(b3_dout), .in4(b4_dout), .in5(b5_dout), .in6(b6_dout),
    .in7(b7_dout), .out(Dout), .sel(Addr[8:6]));
endmodule

module regfile (
  input  clk,
  input  rst,
  input  [31:0] Dwrite,
  input  [4:0] Awrite,
  input  [4:0] Aread0,
  input  [4:0] Aread1,
  output [31:0] Dread0,
  output [31:0] Dread1,
  output [31:0] R1,
  output [31:0] R2,
  output [31:0] R3,
  output [31:0] R4,
  output [31:0] R5,
  output [31:0] R6,
  output [31:0] R7,
  output [31:0] R8,
  output [31:0] R9,
  output [31:0] R10,
  output [31:0] R11,
  output [31:0] R12,
  output [31:0] R13,
  output [31:0] R14,
  output [31:0] R15,
  output [31:0] R16,
  output [31:0] R17,
  output [31:0] R18,
  output [31:0] R19,
  output [31:0] R20,
  output [31:0] R21,
  output [31:0] R22,
  output [31:0] R23,
  output [31:0] R24,
  output [31:0] R25,
  output [31:0] R26,
  output [31:0] R27,
  output [31:0] R28,
  output [31:0] R29,
  output [31:0] R30,
  output [31:0] R31
);

  wire and_1_out, and_2_out, and_3_out, and_4_out, and_5_out, and_6_out, and_7_out, and_8_out, and_9_out,
       and_10_out, and_11_out, and_12_out, and_13_out, and_14_out, and_15_out, and_16_out, and_17_out,
       and_18_out, and_19_out, and_20_out, and_21_out, and_22_out, and_23_out, and_24_out, and_25_out,
       and_26_out, and_27_out, and_28_out, and_29_out, and_30_out, and_31_out, and_32_out, decoder_1_out0,
       decoder_1_out1, decoder_1_out2, decoder_1_out3, decoder_1_out4, decoder_1_out5, decoder_1_out6,
       decoder_1_out7, decoder_2_out0, decoder_2_out1, decoder_2_out2, decoder_2_out3, or_1_out, or_2_out,
       or_3_out, or_4_out, or_5_out, or_6_out, or_7_out, or_8_out, or_9_out, or_10_out, or_11_out, or_12_out,
       or_13_out, or_14_out, or_15_out, or_16_out, or_17_out, or_18_out, or_19_out, or_20_out, or_21_out,
       or_22_out, or_23_out, or_24_out, or_25_out, or_26_out, or_27_out, or_28_out, or_29_out, or_30_out,
       or_31_out, or_32_out, undriven_2, undriven_3, undriven_4, undriven_5;
  wire [31:0] multiplexer_1_out, multiplexer_2_out, multiplexer_3_out, multiplexer_4_out, multiplexer_5_out,
       multiplexer_6_out, multiplexer_7_out, multiplexer_8_out, multiplexer_9_out, undriven;

  Register #(.width(32)) register_1 (.D(undriven), .en(or_1_out), .clk(undriven_2));  // open: Q, clr
  or or_1 (or_1_out, undriven_5, and_1_out);
  and and_1 (and_1_out, undriven_4, undriven_3);
  Decoder #(.select(3)) decoder_1 (
    .out0(decoder_1_out0), .out1(decoder_1_out1), .out2(decoder_1_out2), .out3(decoder_1_out3),
    .out4(decoder_1_out4), .out5(decoder_1_out5), .out6(decoder_1_out6), .out7(decoder_1_out7),
    .sel(Awrite[4:2]));  // open: en
  Decoder #(.select(2)) decoder_2 (
    .out0(decoder_2_out0), .out1(decoder_2_out1), .out2(decoder_2_out2), .out3(decoder_2_out3),
    .sel(Awrite[1:0]));  // open: en
  Multiplexer #(.width(32)) multiplexer_1 (.in0(Dwrite), .in1({32{1'b0}}), .out(multiplexer_1_out), .sel(rst));
  and and_2 (and_2_out, decoder_2_out0, decoder_1_out1);
  and and_3 (and_3_out, decoder_2_out0, decoder_1_out2);
  and and_4 (and_4_out, decoder_2_out0, decoder_1_out3);
  and and_5 (and_5_out, decoder_2_out0, decoder_1_out4);
  and and_6 (and_6_out, decoder_2_out0, decoder_1_out5);
  and and_7 (and_7_out, decoder_2_out0, decoder_1_out6);
  and and_8 (and_8_out, decoder_2_out0, decoder_1_out7);
  Register #(.width(32)) register_2 (.D(multiplexer_1_out), .en(or_2_out), .clk(clk), .Q(R4));  // open: clr
  or or_2 (or_2_out, rst, and_2_out);
  Register #(.width(32)) register_3 (.D(multiplexer_1_out), .en(or_3_out), .clk(clk), .Q(R8));  // open: clr
  or or_3 (or_3_out, rst, and_3_out);
  Register #(.width(32)) register_4 (.D(multiplexer_1_out), .en(or_4_out), .clk(clk), .Q(R12));  // open: clr
  or or_4 (or_4_out, rst, and_4_out);
  Register #(.width(32)) register_5 (.D(multiplexer_1_out), .en(or_5_out), .clk(clk), .Q(R16));  // open: clr
  or or_5 (or_5_out, rst, and_5_out);
  Register #(.width(32)) register_6 (.D(multiplexer_1_out), .en(or_6_out), .clk(clk), .Q(R20));  // open: clr
  or or_6 (or_6_out, rst, and_6_out);
  Register #(.width(32)) register_7 (.D(multiplexer_1_out), .en(or_7_out), .clk(clk), .Q(R24));  // open: clr
  or or_7 (or_7_out, rst, and_7_out);
  Register #(.width(32)) register_8 (.D(multiplexer_1_out), .en(or_8_out), .clk(clk), .Q(R28));  // open: clr
  or or_8 (or_8_out, rst, and_8_out);
  Multiplexer #(.select(3), .width(32)) multiplexer_2 (
    .in0({32{1'b0}}), .in1(R4), .in2(R8), .in3(R12), .in4(R16), .in5(R20), .in6(R24), .in7(R28),
    .out(multiplexer_2_out), .sel(Aread0[4:2]));
  Multiplexer #(.select(3), .width(32)) multiplexer_3 (
    .in0({32{1'b0}}), .in1(R4), .in2(R8), .in3(R12), .in4(R16), .in5(R20), .in6(R24), .in7(R28),
    .out(multiplexer_3_out), .sel(Aread1[4:2]));
  and and_9 (and_9_out, decoder_2_out1, decoder_1_out0);
  and and_10 (and_10_out, decoder_2_out1, decoder_1_out1);
  and and_11 (and_11_out, decoder_2_out1, decoder_1_out2);
  and and_12 (and_12_out, decoder_2_out1, decoder_1_out3);
  and and_13 (and_13_out, decoder_2_out1, decoder_1_out4);
  and and_14 (and_14_out, decoder_2_out1, decoder_1_out5);
  and and_15 (and_15_out, decoder_2_out1, decoder_1_out6);
  and and_16 (and_16_out, decoder_2_out1, decoder_1_out7);
  Register #(.width(32)) register_9 (.D(multiplexer_1_out), .en(or_9_out), .clk(clk), .Q(R1));  // open: clr
  or or_9 (or_9_out, rst, and_9_out);
  Register #(.width(32)) register_10 (.D(multiplexer_1_out), .en(or_10_out), .clk(clk), .Q(R5));  // open: clr
  or or_10 (or_10_out, rst, and_10_out);
  Register #(.width(32)) register_11 (.D(multiplexer_1_out), .en(or_11_out), .clk(clk), .Q(R9));  // open: clr
  or or_11 (or_11_out, rst, and_11_out);
  Register #(.width(32)) register_12 (.D(multiplexer_1_out), .en(or_12_out), .clk(clk), .Q(R13));  // open: clr
  or or_12 (or_12_out, rst, and_12_out);
  Register #(.width(32)) register_13 (.D(multiplexer_1_out), .en(or_13_out), .clk(clk), .Q(R17));  // open: clr
  or or_13 (or_13_out, rst, and_13_out);
  Register #(.width(32)) register_14 (.D(multiplexer_1_out), .en(or_14_out), .clk(clk), .Q(R21));  // open: clr
  or or_14 (or_14_out, rst, and_14_out);
  Register #(.width(32)) register_15 (.D(multiplexer_1_out), .en(or_15_out), .clk(clk), .Q(R25));  // open: clr
  or or_15 (or_15_out, rst, and_15_out);
  Register #(.width(32)) register_16 (.D(multiplexer_1_out), .en(or_16_out), .clk(clk), .Q(R29));  // open: clr
  or or_16 (or_16_out, rst, and_16_out);
  Multiplexer #(.select(3), .width(32)) multiplexer_4 (
    .in0(R1), .in1(R5), .in2(R9), .in3(R13), .in4(R17), .in5(R21), .in6(R25), .in7(R29),
    .out(multiplexer_4_out), .sel(Aread0[4:2]));
  Multiplexer #(.select(3), .width(32)) multiplexer_5 (
    .in0(R1), .in1(R5), .in2(R9), .in3(R13), .in4(R17), .in5(R21), .in6(R25), .in7(R29),
    .out(multiplexer_5_out), .sel(Aread1[4:2]));
  Register #(.width(32)) register_17 (.D(multiplexer_1_out), .en(or_17_out), .clk(clk), .Q(R2));  // open: clr
  or or_17 (or_17_out, rst, and_17_out);
  and and_17 (and_17_out, decoder_2_out2, decoder_1_out0);
  Register #(.width(32)) register_18 (.D(multiplexer_1_out), .en(or_18_out), .clk(clk), .Q(R6));  // open: clr
  or or_18 (or_18_out, rst, and_18_out);
  and and_18 (and_18_out, decoder_2_out2, decoder_1_out1);
  Register #(.width(32)) register_19 (.D(multiplexer_1_out), .en(or_19_out), .clk(clk), .Q(R10));  // open: clr
  or or_19 (or_19_out, rst, and_19_out);
  and and_19 (and_19_out, decoder_2_out2, decoder_1_out2);
  Register #(.width(32)) register_20 (.D(multiplexer_1_out), .en(or_20_out), .clk(clk), .Q(R14));  // open: clr
  or or_20 (or_20_out, rst, and_20_out);
  and and_20 (and_20_out, decoder_2_out2, decoder_1_out3);
  Register #(.width(32)) register_21 (.D(multiplexer_1_out), .en(or_21_out), .clk(clk), .Q(R18));  // open: clr
  or or_21 (or_21_out, rst, and_21_out);
  and and_21 (and_21_out, decoder_2_out2, decoder_1_out4);
  Register #(.width(32)) register_22 (.D(multiplexer_1_out), .en(or_22_out), .clk(clk), .Q(R22));  // open: clr
  or or_22 (or_22_out, rst, and_22_out);
  and and_22 (and_22_out, decoder_2_out2, decoder_1_out5);
  Register #(.width(32)) register_23 (.D(multiplexer_1_out), .en(or_23_out), .clk(clk), .Q(R26));  // open: clr
  or or_23 (or_23_out, rst, and_23_out);
  and and_23 (and_23_out, decoder_2_out2, decoder_1_out6);
  Register #(.width(32)) register_24 (.D(multiplexer_1_out), .en(or_24_out), .clk(clk), .Q(R30));  // open: clr
  or or_24 (or_24_out, rst, and_24_out);
  and and_24 (and_24_out, decoder_2_out2, decoder_1_out7);
  Multiplexer #(.select(3), .width(32)) multiplexer_6 (
    .in0(R2), .in1(R6), .in2(R10), .in3(R14), .in4(R18), .in5(R22), .in6(R26), .in7(R30),
    .out(multiplexer_6_out), .sel(Aread0[4:2]));
  Multiplexer #(.select(3), .width(32)) multiplexer_7 (
    .in0(R2), .in1(R6), .in2(R10), .in3(R14), .in4(R18), .in5(R22), .in6(R26), .in7(R30),
    .out(multiplexer_7_out), .sel(Aread1[4:2]));
  Register #(.width(32)) register_25 (.D(multiplexer_1_out), .en(or_25_out), .clk(clk), .Q(R3));  // open: clr
  or or_25 (or_25_out, rst, and_25_out);
  and and_25 (and_25_out, decoder_2_out3, decoder_1_out0);
  Register #(.width(32)) register_26 (.D(multiplexer_1_out), .en(or_26_out), .clk(clk), .Q(R7));  // open: clr
  or or_26 (or_26_out, rst, and_26_out);
  and and_26 (and_26_out, decoder_2_out3, decoder_1_out1);
  Register #(.width(32)) register_27 (.D(multiplexer_1_out), .en(or_27_out), .clk(clk), .Q(R11));  // open: clr
  or or_27 (or_27_out, rst, and_27_out);
  and and_27 (and_27_out, decoder_2_out3, decoder_1_out2);
  Register #(.width(32)) register_28 (.D(multiplexer_1_out), .en(or_28_out), .clk(clk), .Q(R15));  // open: clr
  or or_28 (or_28_out, rst, and_28_out);
  and and_28 (and_28_out, decoder_2_out3, decoder_1_out3);
  Register #(.width(32)) register_29 (.D(multiplexer_1_out), .en(or_29_out), .clk(clk), .Q(R19));  // open: clr
  or or_29 (or_29_out, rst, and_29_out);
  and and_29 (and_29_out, decoder_2_out3, decoder_1_out4);
  Register #(.width(32)) register_30 (.D(multiplexer_1_out), .en(or_30_out), .clk(clk), .Q(R23));  // open: clr
  or or_30 (or_30_out, rst, and_30_out);
  and and_30 (and_30_out, decoder_2_out3, decoder_1_out5);
  Register #(.width(32)) register_31 (.D(multiplexer_1_out), .en(or_31_out), .clk(clk), .Q(R27));  // open: clr
  or or_31 (or_31_out, rst, and_31_out);
  and and_31 (and_31_out, decoder_2_out3, decoder_1_out6);
  Register #(.width(32)) register_32 (.D(multiplexer_1_out), .en(or_32_out), .clk(clk), .Q(R31));  // open: clr
  or or_32 (or_32_out, rst, and_32_out);
  and and_32 (and_32_out, decoder_2_out3, decoder_1_out7);
  Multiplexer #(.select(3), .width(32)) multiplexer_8 (
    .in0(R3), .in1(R7), .in2(R11), .in3(R15), .in4(R19), .in5(R23), .in6(R27), .in7(R31),
    .out(multiplexer_8_out), .sel(Aread0[4:2]));
  Multiplexer #(.select(3), .width(32)) multiplexer_9 (
    .in0(R3), .in1(R7), .in2(R11), .in3(R15), .in4(R19), .in5(R23), .in6(R27), .in7(R31),
    .out(multiplexer_9_out), .sel(Aread1[4:2]));
  Multiplexer #(.select(2), .width(32)) multiplexer_10 (
    .in0(multiplexer_2_out), .in1(multiplexer_4_out), .in2(multiplexer_6_out), .in3(multiplexer_8_out),
    .out(Dread0), .sel(Aread0[1:0]));
  Multiplexer #(.select(2), .width(32)) multiplexer_11 (
    .in0(multiplexer_3_out), .in1(multiplexer_5_out), .in2(multiplexer_7_out), .in3(multiplexer_9_out),
    .out(Dread1), .sel(Aread1[1:0]));

  // Notes on the sheet:
  //   Field Template
endmodule
